// Logisim project BCD12bit.circ as structural Verilog: 2 circuits, main circuit BCD12BIT
module C1 (
  input  A,
  input  B,
  input  C,
  input  D,
  output S3,
  output S2,
  output S1,
  output S0
);

  wire and_1_out, and_2_out, and_3_out, and_4_out, and_5_out, and_6_out, and_7_out, and_8_out, and_9_out,
       and_10_out, not_1_out, not_2_out, not_3_out, not_4_out, not_5_out, not_6_out, not_7_out, not_8_out;

  and and_1 (and_1_out, B, D);
  and and_2 (and_2_out, B, C);
  and and_3 (and_3_out, B, not_1_out, not_2_out);
  not not_1 (not_1_out, C);
  not not_2 (not_2_out, D);
  and and_4 (and_4_out, A, D);
  not not_3 (not_3_out, B);
  and and_5 (and_5_out, not_3_out, C);
  and and_6 (and_6_out, C, D);
  and and_7 (and_7_out, A, not_4_out);
  not not_4 (not_4_out, D);
  not not_5 (not_5_out, A);
  not not_6 (not_6_out, B);
  and and_8 (and_8_out, not_5_out, not_6_out, D);
  and and_9 (and_9_out, B, C, not_7_out);
  not not_7 (not_7_out, D);
  and and_10 (and_10_out, A, not_8_out);
  not not_8 (not_8_out, D);
  or or_1 (S3, and_1_out, and_2_out, A);
  or or_2 (S2, and_3_out, and_4_out);
  or or_3 (S1, and_5_out, and_6_out, and_7_out);
  or or_4 (S0, and_8_out, and_9_out, and_10_out);
endmodule

module BCD12BIT (
  input  in_1,
  input  in_2,
  input  in_3,
  input  in_4,
  input  in_5,
  input  in_6,
  input  in_7,
  input  in_8,
  input  in_9,
  input  in_10,
  input  in_11,
  input  in_12,
  output out_13,
  output out_14,
  output out_15,
  output out_16,
  output out_17,
  output out_18,
  output out_19,
  output out_20,
  output out_21,
  output out_22,
  output out_23,
  output out_24,
  output out_25,
  output out_26,
  output out_27,
  output out_28
);

  wire c1_1_s0, c1_1_s1, c1_1_s2, c1_1_s3, c1_2_s0, c1_2_s1, c1_2_s2, c1_2_s3, c1_3_s0, c1_3_s1, c1_3_s2,
       c1_3_s3, c1_4_s0, c1_4_s1, c1_4_s2, c1_4_s3, c1_5_s0, c1_5_s1, c1_5_s2, c1_5_s3, c1_6_s0, c1_6_s1,
       c1_6_s2, c1_6_s3, c1_7_s0, c1_7_s1, c1_7_s2, c1_7_s3, c1_8_s0, c1_8_s1, c1_8_s2, c1_8_s3, c1_9_s0,
       c1_9_s1, c1_9_s2, c1_9_s3, c1_10_s0, c1_10_s1, c1_10_s2, c1_10_s3, c1_11_s0, c1_11_s1, c1_11_s2,
       c1_11_s3, c1_12_s0, c1_12_s1, c1_12_s2, c1_13_s0, c1_13_s1, c1_13_s2, c1_14_s0, c1_14_s1, c1_14_s2,
       c1_14_s3, c1_15_s0, c1_15_s1, c1_15_s2, c1_15_s3, c1_16_s0, c1_16_s1, c1_16_s2, c1_16_s3, c1_17_s0,
       c1_17_s1, c1_17_s2, c1_17_s3;

  C1 c1_1 (.A(1'b0), .B(1'b0), .C(in_1), .D(in_2), .S3(c1_1_s3), .S2(c1_1_s2), .S1(c1_1_s1), .S0(c1_1_s0));
  C1 c1_2 (.A(c1_1_s2), .B(c1_1_s1), .C(c1_1_s0), .D(in_3), .S3(c1_2_s3), .S2(c1_2_s2), .S1(c1_2_s1), .S0(c1_2_s0));
  C1 c1_3 (.A(c1_2_s2), .B(c1_2_s1), .C(c1_2_s0), .D(in_4), .S3(c1_3_s3), .S2(c1_3_s2), .S1(c1_3_s1), .S0(c1_3_s0));
  C1 c1_4 (.A(1'b0), .B(c1_1_s3), .C(c1_2_s3), .D(c1_3_s3), .S3(c1_4_s3), .S2(c1_4_s2), .S1(c1_4_s1), .S0(c1_4_s0));
  C1 c1_5 (.A(c1_4_s2), .B(c1_4_s1), .C(c1_4_s0), .D(c1_6_s3), .S3(c1_5_s3), .S2(c1_5_s2), .S1(c1_5_s1), .S0(c1_5_s0));
  C1 c1_6 (.A(c1_3_s2), .B(c1_3_s1), .C(c1_3_s0), .D(in_5), .S3(c1_6_s3), .S2(c1_6_s2), .S1(c1_6_s1), .S0(c1_6_s0));
  C1 c1_7 (.A(c1_6_s2), .B(c1_6_s1), .C(c1_6_s0), .D(in_6), .S3(c1_7_s3), .S2(c1_7_s2), .S1(c1_7_s1), .S0(c1_7_s0));
  C1 c1_8 (.A(c1_5_s2), .B(c1_5_s1), .C(c1_5_s0), .D(c1_7_s3), .S3(c1_8_s3), .S2(c1_8_s2), .S1(c1_8_s1), .S0(c1_8_s0));
  C1 c1_9 (.A(c1_8_s2), .B(c1_8_s1), .C(c1_8_s0), .D(c1_10_s3), .S3(c1_9_s3), .S2(c1_9_s2), .S1(c1_9_s1), .S0(c1_9_s0));
  C1 c1_10 (
    .A(c1_7_s2), .B(c1_7_s1), .C(c1_7_s0), .D(in_7), .S3(c1_10_s3), .S2(c1_10_s2), .S1(c1_10_s1),
    .S0(c1_10_s0));
  C1 c1_11 (
    .A(c1_10_s2), .B(c1_10_s1), .C(c1_10_s0), .D(in_8), .S3(c1_11_s3), .S2(c1_11_s2), .S1(c1_11_s1),
    .S0(c1_11_s0));
  C1 c1_12 (
    .A(c1_4_s3), .B(c1_5_s3), .C(c1_8_s3), .D(c1_9_s3), .S3(out_14), .S2(c1_12_s2), .S1(c1_12_s1),
    .S0(c1_12_s0));
  C1 c1_13 (
    .A(c1_12_s2), .B(c1_12_s1), .C(c1_12_s0), .D(c1_14_s3), .S3(out_15), .S2(c1_13_s2), .S1(c1_13_s1),
    .S0(c1_13_s0));
  C1 c1_14 (
    .A(c1_9_s2), .B(c1_9_s1), .C(c1_9_s0), .D(c1_11_s3), .S3(c1_14_s3), .S2(c1_14_s2), .S1(c1_14_s1),
    .S0(c1_14_s0));
  C1 c1_15 (
    .A(c1_14_s2), .B(c1_14_s1), .C(c1_14_s0), .D(c1_16_s3), .S3(c1_15_s3), .S2(c1_15_s2), .S1(c1_15_s1),
    .S0(c1_15_s0));
  C1 c1_16 (
    .A(c1_11_s2), .B(c1_11_s1), .C(c1_11_s0), .D(in_9), .S3(c1_16_s3), .S2(c1_16_s2), .S1(c1_16_s1),
    .S0(c1_16_s0));
  C1 c1_17 (
    .A(c1_16_s2), .B(c1_16_s1), .C(c1_16_s0), .D(in_10), .S3(c1_17_s3), .S2(c1_17_s2), .S1(c1_17_s1),
    .S0(c1_17_s0));
  C1 c1_18 (.A(c1_13_s2), .B(c1_13_s1), .C(c1_13_s0), .D(c1_15_s3), .S3(out_16), .S2(out_17), .S1(out_18), .S0(out_19));
  C1 c1_19 (.A(c1_15_s2), .B(c1_15_s1), .C(c1_15_s0), .D(c1_17_s3), .S3(out_20), .S2(out_21), .S1(out_22), .S0(out_23));
  C1 c1_20 (.A(c1_17_s2), .B(c1_17_s1), .C(c1_17_s0), .D(in_11), .S3(out_24), .S2(out_25), .S1(out_26), .S0(out_27));

  assign out_13 = 1'b0;
  assign out_28 = in_12;
endmodule
