// Logisim project LAB02.circ as structural Verilog: 10 circuits, main circuit main
// D
module main (
  input  in_1,
  input  in_2,
  input  in_3,
  input  in_4,
  input  in_5,
  input  in_6,
  input  in_7,
  input  in_8,
  input  in_9,
  input  in_10,
  input  in_11,
  input  TESTE_DISPLAY,
  input  in_13,
  input  in_14,
  input  in_15,
  output out_16,
  output out_17,
  output out_18,
  output out_19,
  output out_20,
  output BIN_BCD,
  output out_22,
  output out_23,
  output out_24,
  output out_25,
  output out_26,
  output out_27,
  output out_28,
  output out_29,
  output out_30,
  output out_31,
  output out_32,
  output out_33,
  output out_34,
  output out_35,
  output out_36,
  output out_37,
  output out_38,
  output out_39,
  output out_40,
  output out_41,
  output out_42,
  output out_43,
  output out_44,
  output out_45,
  output out_46,
  output out_47,
  output out_48,
  output out_49,
  output out_50,
  output out_51,
  output out_52,
  output out_53,
  output out_54,
  output out_55
);

  wire A, A1, A2, B, B1, B2, C, C1, C2, clock_1_out, D, D1, D2, E, E1, E2, F, F1, F2, G, G1, G2;
  wire [7:0] counter_1_q;

  Counter #(.behavior("old")) counter_1 (
    .Q(counter_1_q), .clk(clock_1_out));  // open: load, D, count, carry, clr, preset
  Clock clock_1 (.out(clock_1_out));
  C1 u_C1 (.A(1'b0), .B(in_1), .C(in_2), .D(in_3), .S3(out_16), .S2(out_17), .S1(out_18), .S0(out_19));
  C1 C4 (.A(1'b0), .B(out_16), .C(out_20), .D(out_24), .S3(out_28), .S2(out_29), .S1(out_30), .S0(out_31));
  C1 C5 (.A(out_25), .B(out_26), .C(out_27), .D(in_6), .S3(out_36), .S2(out_37), .S1(out_38), .S0(out_39));
  C1 u_C2 (.A(out_17), .B(out_18), .C(out_19), .D(in_4), .S3(out_20), .S2(BIN_BCD), .S1(out_22), .S0(out_23));
  C1 C6 (.A(out_29), .B(out_30), .C(out_31), .D(out_36), .S3(out_32), .S2(out_33), .S1(out_34), .S0(out_35));
  C1 C7 (.A(out_37), .B(out_38), .C(out_39), .D(in_7), .S3(out_40), .S2(out_41), .S1(out_42), .S0(out_43));
  C1 C3 (.A(BIN_BCD), .B(out_22), .C(out_23), .D(in_5), .S3(out_24), .S2(out_25), .S1(out_26), .S0(out_27));
  Cod cod_1 (
    .in_1(1'b0), .in_2(1'b0), .in_3(out_28), .in_4(out_32), .A(A2), .B(B2), .C(C2), .D(D2), .E(E2), .F(F2),
    .G(G2));
  Cod cod_2 (
    .in_1(out_33), .in_2(out_34), .in_3(out_35), .in_4(out_40), .A(A1), .B(B1), .C(C1), .D(D1), .E(E1),
    .F(F1), .G(G1));
  Cod cod_3 (.in_1(out_41), .in_2(out_42), .in_3(out_43), .in_4(in_8), .A(A), .B(B), .C(C), .D(D), .E(E), .F(F), .G(G));
  _7_Segment_Display #(.active("false")) u_7_segment_display_1 (
    .g(G2), .f(F2), .a(A2), .b(B2), .e(E2), .d(D2), .c(C2));  // open: dp
  _7_Segment_Display #(.active("false")) u_7_segment_display_2 (
    .g(G1), .f(F1), .a(A1), .b(B1), .e(E1), .d(D1), .c(C1));  // open: dp
  _7_Segment_Display u_7_segment_display_3 (
    .g(in_9), .f(in_10), .a(in_15), .b(in_14), .e(in_11), .d(TESTE_DISPLAY), .c(in_13));  // open: dp
  _7_Segment_Display #(.active("false")) u_7_segment_display_4 (
    .g(G), .f(F), .a(A), .b(B), .e(E), .d(D), .c(C));  // open: dp

  assign out_44 = 1'b0;
  assign out_45 = 1'b0;
  assign out_46 = out_28;
  assign out_47 = out_32;
  assign out_48 = out_33;
  assign out_49 = out_34;
  assign out_50 = out_35;
  assign out_51 = out_40;
  assign out_52 = out_41;
  assign out_53 = out_42;
  assign out_54 = out_43;
  assign out_55 = in_8;

  // Other names for the same wires on the sheet: c1s0 = out_19; c1s1 = out_18; c1s2 = out_17; c1s3 = out_16;
  //   c2s0 = out_23; c2s1 = out_22; c2s2 = BIN_BCD; c2s3 = out_20; c3s0 = out_27; c3s1 = out_26; c3s2 = out_25;
  //   c3s3 = out_24; c4s0 = out_31; c4s1 = out_30; c4s2 = out_29; c4s3 = out_28; c5s0 = out_39; c5s1 = out_38;
  //   c5s2 = out_37; c5s3 = out_36; c6s0 = out_35; c6s1 = out_34; c6s2 = out_33; c6s3 = out_32; c7s0 = out_43;
  //   c7s1 = out_42; c7s2 = out_41; c7s3 = out_40; D0 = in_15; D3 = TESTE_DISPLAY; D4 = in_11; D5 = in_10; D6 = in_9;
  //   D71 = in_14; D72 = in_13; sw0 = in_8; sw1 = in_7; sw2 = in_6; sw3 = in_5; sw4 = in_4; sw5 = in_3; sw6 = in_2;
  //   sw7 = in_1

  // Notes on the sheet:
  //   ENTRADA 8 BITS:
  //   AUTO INPUT:
  //   SAIDA BIN-BCD:
  //   SAIDA DO DISPLAY:
endmodule

module C1 (
  input  A,
  input  B,
  input  C,
  input  D,
  output S3,
  output S2,
  output S1,
  output S0
);

  wire and_1_out, and_2_out, and_3_out, and_4_out, and_5_out, and_6_out, and_7_out, and_8_out, and_9_out,
       and_10_out, not_1_out, not_2_out, not_3_out, not_4_out, not_5_out, not_6_out, not_7_out, not_8_out;

  and and_1 (and_1_out, B, D);
  and and_2 (and_2_out, B, C);
  not not_1 (not_1_out, C);
  and and_3 (and_3_out, B, not_1_out, not_2_out);
  not not_2 (not_2_out, D);
  and and_4 (and_4_out, A, D);
  not not_3 (not_3_out, B);
  and and_5 (and_5_out, not_3_out, C);
  and and_6 (and_6_out, C, D);
  and and_7 (and_7_out, A, not_4_out);
  not not_4 (not_4_out, D);
  not not_5 (not_5_out, A);
  and and_8 (and_8_out, not_5_out, not_6_out, D);
  not not_6 (not_6_out, B);
  and and_9 (and_9_out, B, C, not_7_out);
  not not_7 (not_7_out, D);
  and and_10 (and_10_out, A, not_8_out);
  not not_8 (not_8_out, D);
  or or_1 (S3, and_1_out, and_2_out, A);
  or or_2 (S2, and_3_out, and_4_out);
  or or_3 (S1, and_5_out, and_6_out, and_7_out);
  or or_4 (S0, and_8_out, and_9_out, and_10_out);
endmodule

module SegA (
  input  a,
  input  b,
  input  c,
  input  d,
  output sa
);

  wire and_1_out, and_2_out, not_1_out, not_2_out, not_3_out, not_4_out, not_5_out;

  not not_1 (not_1_out, a);
  not not_2 (not_2_out, b);
  not not_3 (not_3_out, c);
  not not_4 (not_4_out, c);
  not not_5 (not_5_out, d);
  and and_1 (and_1_out, not_1_out, not_2_out, not_3_out, d);
  or or_1 (sa, and_1_out, and_2_out);
  and and_2 (and_2_out, b, not_4_out, not_5_out);
endmodule

module SegB (
  input  a,
  input  b,
  input  c,
  input  d,
  output sb
);

  wire and_1_out, and_2_out, not_1_out, not_2_out;

  and and_1 (and_1_out, b, not_1_out, d);
  not not_1 (not_1_out, c);
  and and_2 (and_2_out, b, c, not_2_out);
  not not_2 (not_2_out, d);
  or or_1 (sb, and_1_out, and_2_out);
endmodule

module SegC (
  input  a,
  input  b,
  input  c,
  input  d,
  output sc
);

  wire not_1_out, not_2_out;

  not not_1 (not_1_out, b);
  and and_1 (sc, not_1_out, c, not_2_out);
  not not_2 (not_2_out, d);
endmodule

module SegD (
  input  a,
  input  b,
  input  c,
  input  d,
  output sd
);

  wire and_1_out, and_2_out, and_3_out, not_1_out, not_2_out, not_3_out, not_4_out, not_5_out;

  not not_1 (not_1_out, a);
  not not_2 (not_2_out, b);
  not not_3 (not_3_out, c);
  not not_4 (not_4_out, c);
  not not_5 (not_5_out, d);
  and and_1 (and_1_out, not_1_out, not_2_out, not_3_out, d);
  or or_1 (sd, and_1_out, and_2_out, and_3_out);
  and and_2 (and_2_out, b, not_4_out, not_5_out);
  and and_3 (and_3_out, b, c, d);
endmodule

module SegE (
  input  a,
  input  b,
  input  c,
  input  d,
  output se
);

  wire and_1_out, not_1_out;

  and and_1 (and_1_out, b, not_1_out);
  not not_1 (not_1_out, c);
  or or_1 (se, d, and_1_out);
endmodule

module SegF (
  input  a,
  input  b,
  input  c,
  input  d,
  output sf
);

  wire and_1_out, and_2_out, and_3_out, not_1_out, not_2_out, not_3_out;

  not not_1 (not_1_out, a);
  not not_2 (not_2_out, b);
  and and_1 (and_1_out, not_1_out, not_2_out, d);
  not not_3 (not_3_out, b);
  and and_2 (and_2_out, not_3_out, c);
  and and_3 (and_3_out, c, d);
  or or_1 (sf, and_1_out, and_2_out, and_3_out);
endmodule

module SegG (
  input  a,
  input  b,
  input  c,
  input  d,
  output sg
);

  wire and_1_out, and_2_out, not_1_out, not_2_out, not_3_out;

  not not_1 (not_1_out, a);
  and and_1 (and_1_out, not_1_out, not_2_out, not_3_out);
  not not_2 (not_2_out, b);
  not not_3 (not_3_out, c);
  and and_2 (and_2_out, b, c, d);
  or or_1 (sg, and_1_out, and_2_out);
endmodule

module Cod (
  input  in_1,
  input  in_2,
  input  in_3,
  input  in_4,
  output A,
  output B,
  output C,
  output D,
  output E,
  output F,
  output G
);

  SegA sega_1 (.a(in_1), .b(in_2), .c(in_3), .d(in_4), .sa(A));
  SegB segb_1 (.a(in_1), .b(in_2), .c(in_3), .d(in_4), .sb(B));
  SegC segc_1 (.a(in_1), .b(in_2), .c(in_3), .d(in_4), .sc(C));
  SegD segd_1 (.a(in_1), .b(in_2), .c(in_3), .d(in_4), .sd(D));
  SegE sege_1 (.a(in_1), .b(in_2), .c(in_3), .d(in_4), .se(E));
  SegF segf_1 (.a(in_1), .b(in_2), .c(in_3), .d(in_4), .sf(F));
  SegG segg_1 (.a(in_1), .b(in_2), .c(in_3), .d(in_4), .sg(G));

  // Other names for the same wires on the sheet: A1 = in_1; A2 = in_2; A3 = in_3; A4 = in_4
endmodule
