// Logisim project LAB03.circ as structural Verilog
module main (
  input  Sinal,
  input  in_2,
  input  Input,
  input  in_4,
  input  in_5,
  output Input_2,
  output out_7,
  output out_8,
  output NOT,
  output out_10,
  output out_11,
  output plus_1,
  output out_13,
  output out_14
);

  wire A, B, C, clock_1_out, D, E, F, G, Logica_sa, Logica_sb, Logica_sc, Logica_sd, S_prime;
  wire [3:0] counter_1_q;

  LOGICA Logica (
    .S(S_prime), .A(Input_2), .B(out_7), .C(out_8), .SA(Logica_sa), .SB(Logica_sb), .SC(Logica_sc),
    .SD(Logica_sd));
  _7_Segment_Display u_7_segment_display_1 (.g(G), .f(F), .a(A), .b(B), .e(E), .d(D), .c(C), .dp(1'b0));
  LED led_1 (.in(S_prime));
  TTL7448 TTL7448 (
    .in_1(Logica_sa), .in_2(Logica_sb), .in_3(Logica_sc), .in_4(Logica_sd), .out_5(A), .out_6(B), .out_7(C),
    .out_8(D), .out_9(E), .out_10(F), .out_11(G));
  Quadrado quadrado_1 ();
  not not_1 (out_11, out_8);
  not not_2 (out_10, out_7);
  not not_3 (NOT, Input_2);
  Soma soma_1 (.in_1(out_11), .in_2(out_10), .in_3(NOT), .out_4(out_14), .out_5(out_13), .out_6(plus_1));
  Quadrado quadrado_2 ();
  Clock clock_1 (.out(clock_1_out));
  Transistor #(.\type ("n")) transistor_1 (.in(counter_1_q[0]), .out(out_8), .gate(Sinal));
  Transistor #(.\type ("n")) transistor_2 (.in(counter_1_q[1]), .out(out_7), .gate(Sinal));
  Transistor #(.\type ("n")) transistor_3 (.in(counter_1_q[2]), .out(Input_2), .gate(Sinal));
  Transistor #(.\type ("n")) transistor_4 (.in(counter_1_q[3]), .out(S_prime), .gate(Sinal));
  Counter #(.width(4), .max('hf)) counter_1 (
    .Q(counter_1_q), .clk(clock_1_out));  // open: load, D, count, carry, clr, preset, down
  Transistor transistor_5 (.in(in_5), .out(out_8), .gate(Sinal));
  Transistor transistor_6 (.in(in_4), .out(out_7), .gate(Sinal));
  Transistor transistor_7 (.in(Input), .out(Input_2), .gate(Sinal));
  Transistor transistor_8 (.in(in_2), .out(S_prime), .gate(Sinal));

  // Other names for the same wires on the sheet: b0 = out_8; b1 = out_7; b2 = Input_2; I0 = in_5; I1 = in_4;
  //   I2 = Input; K = Sinal; S = in_2

  // Notes on the sheet:
  //   Seletor de Input:
  //   Circuito:
  //   LAB03 - Modulo de um Numero:
  //   Complemento A2:
  //   Para determinar o negativo de um número,
  //   inverte-se todos os seus bits e soma-se uma unidade.
  //   Circuito de Chaveamento:
endmodule

module TTL7448 (
  input  in_1,
  input  in_2,
  input  in_3,
  input  in_4,
  output out_5,
  output out_6,
  output out_7,
  output out_8,
  output out_9,
  output out_10,
  output out_11
);

  // DisplayDecoder displaydecoder_1: pin names not known; wires that end beside it: {in_1, in_2, in_3, in_4}, out_5, out_6, out_7, out_8, out_9, out_10, out_11
endmodule

module LOGICA (
  input  S,
  input  A,
  input  B,
  input  C,
  output SA,
  output SB,
  output SC,
  output SD
);

  wire and_3_out, and_4_out, and_5_out, and_6_out, and_7_out, and_8_out, and_9_out, and_11_out,
       B_prime_C_prime, C_prime, not_1_out, not_2_out, not_3_out, not_4_out, not_6_out, or_1_out, or_3_out,
       or_4_out, SA_prime;

  and and_1 (SA_prime, S, not_1_out);
  not not_1 (not_1_out, A);
  not not_2 (not_2_out, B);
  and and_2 (B_prime_C_prime, not_2_out, C_prime);
  not not_3 (not_3_out, S);
  and and_3 (and_3_out, not_3_out, A);
  and and_4 (and_4_out, A, B_prime_C_prime);
  and and_5 (and_5_out, SA_prime, C);
  and and_6 (and_6_out, SA_prime, B);
  not not_4 (not_4_out, S);
  and and_7 (and_7_out, not_4_out, B);
  and and_8 (and_8_out, B, C_prime);
  not not_5 (C_prime, C);
  and and_9 (and_9_out, S, not_6_out);
  not not_6 (not_6_out, B);
  and and_10 (SA, SA_prime, B_prime_C_prime);
  or or_1 (or_1_out, and_3_out, and_4_out);
  or or_2 (SB, or_1_out, or_3_out);
  or or_3 (or_3_out, and_5_out, and_6_out);
  or or_4 (or_4_out, and_7_out, and_8_out);
  or or_5 (SC, or_4_out, and_11_out);
  and and_11 (and_11_out, and_9_out, C);

  assign SD = C;

  // Notes on the sheet:
  //   S A' B' C'
  //   S' A + A B' C' 
  //   + S A' C + S A' B
  //   S' B + B C' + S B' C
  //   C
endmodule

module Soma (
  input  in_1,
  input  in_2,
  input  in_3,
  output out_4,
  output out_5,
  output out_6
);

  wire and_1_out, and_2_out, and_3_out, and_4_out, and_5_out, and_6_out, and_7_out, and_8_out, and_9_out, C0,
       C1, C2;

  and and_1 (and_1_out, in_1, 1'b0);
  and and_2 (and_2_out, in_1, 1'b1);
  and and_3 (and_3_out, 1'b0, 1'b1);
  xor xor_1 (out_4, in_1, 1'b1, 1'b0);
  or or_1 (C0, and_1_out, and_2_out, and_3_out);
  and and_4 (and_4_out, in_2, 1'b0);
  and and_5 (and_5_out, in_2, C0);
  and and_6 (and_6_out, 1'b0, C0);
  xor xor_2 (out_5, in_2, C0, 1'b0);
  or or_2 (C1, and_4_out, and_5_out, and_6_out);
  and and_7 (and_7_out, in_3, 1'b0);
  and and_8 (and_8_out, in_3, C1);
  and and_9 (and_9_out, 1'b0, C1);
  xor xor_3 (out_6, in_3, C1, 1'b0);
  or or_3 (C2, and_7_out, and_8_out, and_9_out);

  // Other names for the same wires on the sheet: A = in_1; A1 = in_2; A2 = in_3; S0 = out_4; S1 = out_5; S2 = out_6
endmodule

module NOT (
  input  A1,
  input  B1,
  input  V2,
  output A,
  output B,
  output C
);

  not not_1 (B, B1);
  not not_2 (A, A1);
  not not_3 (C, V2);
endmodule
