// Logisim project LAB04.circ as structural Verilog: 5 circuits, main circuit main
module main (
  input  in_1,
  input  in_2,
  input  in_3,
  input  in_4,
  input  in_5,
  input  in_6,
  input  in_7,
  input  in_8,
  input  in_9,
  input  in_10,
  output out_11,
  output out_12,
  output out_13,
  output out_14,
  output out_15,
  output out_16,
  output out_17
);

  wire CO, comp4bits_1_a_plus, comp4bits_1_b_plus, DA1, DA2, DB1, DB2, DC1, DC2, DD1, DD2, DE1, DE2, DEN3,
       DF1, DF2, DG1, DG2, or_1_out, S0, S0N, S1, S1N, S2, S2N, S3, S3N;

  _7_Segment_Display u_7_segment_display_1 (.g(DG2), .f(DF2), .a(DA2), .b(DB2), .e(DE2), .d(DD2), .c(DC2), .dp(1'b0));
  COMP4bits comp4bits_1 (
    .in_1(1'b0), .in_2(CO), .in_3(1'b1), .in_4(S3), .in_5(1'b0), .in_6(S2), .in_7(1'b0), .in_8(S1),
    .A_plus(comp4bits_1_a_plus), .B_plus(comp4bits_1_b_plus), .in_9(1'b1), .in_10(S0));  // open: out_11
  Adder #(.width(4)) adder_1 (
    .a({in_5, in_6, in_7, in_8}), .b({in_1, in_2, in_3, in_4}), .out({S3, S2, S1, S0}), .cin(in_9), .cout(CO));
  or or_1 (or_1_out, comp4bits_1_a_plus, comp4bits_1_b_plus);
  _7_Segment_Display u_7_segment_display_2 (.g(DG1), .f(DF1), .a(DA1), .b(DB1), .e(DE1), .d(DD1), .c(DC1), .dp(1'b0));
  Multiplexer #(.enable("false")) multiplexer_1 (.in0(S3), .in1(S3N), .out(out_14), .sel(or_1_out));
  Multiplexer #(.enable("false")) multiplexer_2 (.in0(S2), .in1(S2N), .out(out_15), .sel(or_1_out));
  _7447 #(.ShowInternalStructure("true")) u_7447_1 (
    .pin1(out_12), .pin2(out_11), .pin6(DEN3), .pin7(out_13), .pin15(DF2), .pin14(DG2), .pin13(DA2),
    .pin12(DB2), .pin11(DC2), .pin10(DD2), .pin9(DE2));  // open: pin3, pin4, pin5
  Multiplexer #(.enable("false")) multiplexer_3 (.in0(S1), .in1(S1N), .out(out_16), .sel(or_1_out));
  Multiplexer #(.enable("false")) multiplexer_4 (.in0(S0), .in1(S0N), .out(out_17), .sel(or_1_out));
  Adder #(.width(7)) adder_2 (
    .a({2'b00, CO, S3, S2, S1, S0}), .b(7'b0000110), .out({out_11, out_12, out_13, S3N, S2N, S1N, S0N}),
    .cin(in_10));  // open: cout
  _7447 #(.ShowInternalStructure("true")) u_7447_2 (
    .pin1(out_16), .pin2(out_15), .pin6(out_14), .pin7(out_17), .pin15(DF1), .pin14(DG1), .pin13(DA1),
    .pin12(DB1), .pin11(DC1), .pin10(DD1), .pin9(DE1));  // open: pin3, pin4, pin5
  // also tied to GND on the sheet: DEN3

  // Other names for the same wires on the sheet: DEN0 = out_13; S4N = out_13; DEN1 = out_12; S5N = out_12;
  //   DEN2 = out_11; S6N = out_11; UN0 = out_17; UN1 = out_16; UN2 = out_15; UN3 = out_14
endmodule

module main_2 (
  input  in_1,
  input  in_2,
  input  in_3,
  input  in_4,
  input  in_5,
  input  in_6,
  input  in_7,
  input  in_8,
  input  in_9,
  output out_10,
  output out_11,
  output out_12,
  output out_13,
  output out_14,
  output out_15,
  output out_16,
  output out_17
);

  wire adder_1_cout, DA1, DA2, DB1, DB2, DC1, DC2, DD1, DD2, DE1, DE2, DF1, DF2, DG1, DG2;
  wire [3:0] adder_1_out;

  Adder #(.width(4)) adder_1 (
    .a({in_6, in_7, in_8, in_9}), .b({in_2, in_3, in_4, in_5}), .out(adder_1_out), .cin(in_1),
    .cout(adder_1_cout));
  conv_6 conv_6_1 (
    .A(adder_1_cout), .B(adder_1_out[3]), .C(adder_1_out[2]), .D(adder_1_out[1]), .E(adder_1_out[0]),
    .CO(out_13), .S0(out_14), .S1(out_15), .S2(out_16), .S3(out_17));
  _7_Segment_Display u_7_segment_display_1 (.g(DG2), .f(DF2), .a(DA2), .b(DB2), .e(DE2), .d(DD2), .c(DC2), .dp(1'b0));
  _7447 #(.ShowInternalStructure("true")) u_7447_1 (
    .pin1(out_12), .pin2(out_11), .pin6(out_10), .pin7(out_13), .pin15(DF2), .pin14(DG2), .pin13(DA2),
    .pin12(DB2), .pin11(DC2), .pin10(DD2), .pin9(DE2));  // open: pin3, pin4, pin5
  _7_Segment_Display u_7_segment_display_2 (.g(DG1), .f(DF1), .a(DA1), .b(DB1), .e(DE1), .d(DD1), .c(DC1), .dp(1'b0));
  _7447 #(.ShowInternalStructure("true")) u_7447_2 (
    .pin1(out_16), .pin2(out_15), .pin6(out_14), .pin7(out_17), .pin15(DF1), .pin14(DG1), .pin13(DA1),
    .pin12(DB1), .pin11(DC1), .pin10(DD1), .pin9(DE1));  // open: pin3, pin4, pin5
  // also tied to GND on the sheet: {out_12, out_11, out_10}

  // Other names for the same wires on the sheet: DEN0 = out_13; DEN1 = out_12; DEN2 = out_11; DEN3 = out_10;
  //   UN0 = out_17; UN1 = out_16; UN2 = out_15; UN3 = out_14
endmodule

module COMP (
  input  A_B,
  input  A,
  input  B,
  input  A_B_2,
  input  A_B_3,
  output S_A_B,
  output S_A_B_2,
  output S_A_B_3
);

  wire and_2_out, and_3_out, and_4_out, and_5_out, xnor_1_out;

  and and_1 (S_A_B, A_B, xnor_1_out);
  xnor xnor_1 (xnor_1_out, A, B);
  and and_2 (and_2_out, A_B, and_3_out);
  and and_3 (and_3_out, ~B, A);  // AND_Gate
  and and_4 (and_4_out, A_B, and_5_out);
  and and_5 (and_5_out, B, ~A);  // AND_Gate
  or or_1 (S_A_B_2, and_2_out, A_B_2);
  or or_2 (S_A_B_3, and_4_out, A_B_3);
endmodule

module COMP4bits (
  input  in_1,
  input  in_2,
  input  in_3,
  input  in_4,
  input  in_5,
  input  in_6,
  input  in_7,
  input  in_8,
  input  in_9,
  input  in_10,
  output out_11,
  output A_plus,
  output B_plus
);

  wire comp_1_s_a_b, comp_1_s_a_b_2, comp_1_s_a_b_3, comp_2_s_a_b, comp_2_s_a_b_2, comp_2_s_a_b_3,
       comp_3_s_a_b, comp_3_s_a_b_2, comp_3_s_a_b_3, comp_4_s_a_b, comp_4_s_a_b_2, comp_4_s_a_b_3;

  COMP comp_1 (
    .A_B(1'b1), .A(in_1), .B(in_2), .A_B_2(1'b0), .A_B_3(1'b0), .S_A_B(comp_1_s_a_b),
    .S_A_B_2(comp_1_s_a_b_2), .S_A_B_3(comp_1_s_a_b_3));
  COMP comp_2 (
    .A_B(comp_1_s_a_b), .A(in_3), .B(in_4), .A_B_2(comp_1_s_a_b_2), .A_B_3(comp_1_s_a_b_3),
    .S_A_B(comp_2_s_a_b), .S_A_B_2(comp_2_s_a_b_2), .S_A_B_3(comp_2_s_a_b_3));
  COMP comp_3 (
    .A_B(comp_2_s_a_b), .A(in_5), .B(in_6), .A_B_2(comp_2_s_a_b_2), .A_B_3(comp_2_s_a_b_3),
    .S_A_B(comp_3_s_a_b), .S_A_B_2(comp_3_s_a_b_2), .S_A_B_3(comp_3_s_a_b_3));
  COMP comp_4 (
    .A_B(comp_3_s_a_b), .A(in_7), .B(in_8), .A_B_2(comp_3_s_a_b_2), .A_B_3(comp_3_s_a_b_3),
    .S_A_B(comp_4_s_a_b), .S_A_B_2(comp_4_s_a_b_2), .S_A_B_3(comp_4_s_a_b_3));
  COMP comp_5 (
    .A_B(comp_4_s_a_b), .A(in_9), .B(in_10), .A_B_2(comp_4_s_a_b_2), .A_B_3(comp_4_s_a_b_3), .S_A_B(out_11),
    .S_A_B_2(A_plus), .S_A_B_3(B_plus));
endmodule

module conv_6 (
  input  A,
  input  B,
  input  C,
  input  D,
  input  E,
  output CO,
  output S0,
  output S1,
  output S2,
  output S3
);

  wire and_1_out, and_2_out, and_3_out, and_4_out, and_5_out, and_6_out, and_7_out, and_8_out, and_9_out,
       and_10_out, and_11_out, and_12_out, and_13_out, not_1_out, not_2_out, not_3_out, not_4_out, not_5_out,
       not_6_out, not_7_out, not_8_out, not_9_out, not_10_out, not_11_out, not_12_out, not_13_out,
       not_14_out, not_15_out, not_16_out, not_17_out, not_18_out, not_19_out, not_20_out, not_21_out,
       not_22_out, not_23_out, not_24_out, not_25_out;

  not not_1 (not_1_out, A);
  not not_2 (not_2_out, A);
  not not_3 (not_3_out, B);
  not not_4 (not_4_out, C);
  not not_5 (not_5_out, A);
  not not_6 (not_6_out, C);
  not not_7 (not_7_out, D);
  not not_8 (not_8_out, B);
  not not_9 (not_9_out, C);
  not not_10 (not_10_out, A);
  not not_11 (not_11_out, B);
  not not_12 (not_12_out, A);
  not not_13 (not_13_out, B);
  not not_14 (not_14_out, C);
  not not_15 (not_15_out, D);
  not not_16 (not_16_out, A);
  not not_17 (not_17_out, B);
  not not_18 (not_18_out, A);
  not not_19 (not_19_out, D);
  not not_20 (not_20_out, B);
  not not_21 (not_21_out, C);
  not not_22 (not_22_out, D);
  not not_23 (not_23_out, A);
  not not_24 (not_24_out, B);
  not not_25 (not_25_out, C);
  and and_1 (and_1_out, not_1_out, B, D);
  and and_2 (and_2_out, not_2_out, B, C);
  and and_3 (and_3_out, A, not_3_out, not_4_out);
  and and_4 (and_4_out, not_5_out, B, not_6_out, not_7_out);
  and and_5 (and_5_out, A, not_8_out, not_9_out, D);
  and and_6 (and_6_out, not_10_out, not_11_out, C);
  and and_7 (and_7_out, not_12_out, C, D);
  and and_8 (and_8_out, A, not_13_out, not_14_out, not_15_out);
  and and_9 (and_9_out, not_16_out, not_17_out, D);
  and and_10 (and_10_out, not_18_out, B, C, not_19_out);
  and and_11 (and_11_out, A, not_20_out, not_21_out, not_22_out);
  and and_12 (and_12_out, not_23_out, E);
  and and_13 (and_13_out, not_24_out, not_25_out, E);
  or or_1 (CO, and_1_out, and_2_out, and_3_out);
  or or_2 (S0, and_4_out, and_5_out);
  or or_3 (S1, and_6_out, and_7_out, and_8_out);
  or or_4 (S2, and_9_out, and_10_out, and_11_out);
  or or_5 (S3, and_12_out, and_13_out);
endmodule
