// Logisim project LAB05.circ as structural Verilog: 3 circuits, main circuit main
module main (
  input  in_1,
  input  in_2,
  input  in_3,
  input  in_4,
  input  in_5,
  input  in_6,
  input  in_7,
  output out_8,
  output out_9,
  output out_10,
  output out_11
);

  wire circuito_y_1_out_13, CLK, DA1, DB1, DC1, DD1, DE1, DF1, DG1, UN0, UN1, UN2, UN3;

  Clock clock_1 (.out(CLK));
  Circuito_X circuito_x_1 (
    .CLR(CLK), .BIT_IN(circuito_y_1_out_13), .CLRN(in_3), .B0(UN0), .B1(UN1), .B2(UN2), .B3(UN3));
  _7_Segment_Display u_7_segment_display_1 (.g(DG1), .f(DF1), .a(DA1), .b(DB1), .e(DE1), .d(DD1), .c(DC1), .dp(1'b0));
  Circuito_Y circuito_y_1 (
    .in_1(in_1), .in_2(in_2), .in_3(in_3), .in_4(CLK), .out_13(circuito_y_1_out_13), .in_5(in_4),
    .in_6(in_5), .in_7(in_6), .in_8(in_7), .out_9(out_11), .out_10(out_10), .out_11(out_9), .out_12(out_8));
  _7447 #(.ShowInternalStructure("true")) u_7447_1 (
    .pin1(UN1), .pin2(UN2), .pin6(UN3), .pin7(UN0), .pin15(DF1), .pin14(DG1), .pin13(DA1), .pin12(DB1),
    .pin11(DC1), .pin10(DD1), .pin9(DE1));  // open: pin3, pin4, pin5

  // Other names for the same wires on the sheet: B0 = in_7; B1 = in_6; B2 = in_5; B3 = in_4; LD = in_2; RESET = in_3;
  //   SHL = in_1
endmodule

module Circuito_X (
  input  CLR,
  input  BIT_IN,
  input  CLRN,
  output B0,
  output B1,
  output B2,
  output B3
);

  D_Flip_Flop d_ff_1 (.clk(CLR), .D(BIT_IN), .Q(B0), .reset(CLRN));  // open: Qn, preset
  D_Flip_Flop d_ff_2 (.clk(CLR), .D(B0), .Q(B1), .reset(CLRN));  // open: Qn, preset
  D_Flip_Flop d_ff_3 (.clk(CLR), .D(B1), .Q(B2), .reset(CLRN));  // open: Qn, preset
  D_Flip_Flop d_ff_4 (.clk(CLR), .D(B2), .Q(B3), .reset(CLRN));  // open: Qn, preset
endmodule

module Circuito_Y (
  input  in_1,
  input  in_2,
  input  in_3,
  input  in_4,
  input  in_5,
  input  in_6,
  input  in_7,
  input  in_8,
  output out_9,
  output out_10,
  output out_11,
  output out_12,
  output out_13
);

  wire and_1_out, and_2_out, and_3_out, and_4_out, CLK;

  and and_1 (and_1_out, in_2, in_8);
  D_Flip_Flop d_ff_1 (.clk(CLK), .D(1'b0), .Q(out_9), .preset(and_1_out), .reset(in_3));  // open: Qn
  and and_2 (and_2_out, in_2, in_7);
  D_Flip_Flop d_ff_2 (.clk(CLK), .D(out_9), .Q(out_10), .preset(and_2_out), .reset(in_3));  // open: Qn
  Multiplexer #(.enable("false")) multiplexer_1 (.in0(1'b0), .in1(in_4), .out(CLK), .sel(in_1));
  and and_3 (and_3_out, in_2, in_6);
  D_Flip_Flop d_ff_3 (.clk(CLK), .D(out_10), .Q(out_11), .preset(and_3_out), .reset(in_3));  // open: Qn
  and and_4 (and_4_out, in_2, in_5);
  D_Flip_Flop d_ff_4 (.clk(CLK), .D(out_11), .Q(out_12), .preset(and_4_out), .reset(in_3));  // open: Qn

  assign out_13 = out_12;

  // Other names for the same wires on the sheet: B0 = in_8; B1 = in_7; B2 = in_6; B3 = in_5; CLK0 = in_4; LD = in_2;
  //   RESET = in_3; SHL = in_1
endmodule
