// Logisim project LAB06.circ as structural Verilog
module main (
  input  in_1,
  input  in_2,
  input  in_3,
  input  in_4,
  input  in_5,
  input  in_6,
  input  in_7,
  input  in_8,
  input  in_9,
  input  in_10
);

  wire a_b, and_1_out, and_2_out, and_3_out, and_4_out, CLK, comparator_2_eq, comparator_3_eq, D0, D1, D2,
       D3, d_ff_1_q, DA1, DB1, DC1, DD1, DE1, DF1, DG1, Ena, j_k_ff_1_qn, j_k_ff_2_qn, j_k_ff_3_qn,
       j_k_ff_4_qn, LM, multiplexer_5_out, multiplexer_10_out, multiplexer_11_out, not_1_out, not_2_out, S0,
       S1, S2, S3, U0, U1, U2, U3, xor_1_out;

  Clock clock_1 (.out(CLK));
  Comparator #(.width(4), .mode("unsigned")) comparator_1 (
    .a({in_2, in_3, in_4, in_5}), .b({in_6, in_7, in_8, in_9}), .gt(a_b));  // open: eq, lt
  and and_1 (and_1_out, in_1, D0);
  J_K_Flip_Flop #(.enable("true")) j_k_ff_1 (
    .J(Ena), .clk(CLK), .K(Ena), .Q(S0), .Qn(j_k_ff_1_qn), .preset(and_1_out), .en(Ena), .reset(in_10));
  Multiplexer #(.enable("false")) multiplexer_1 (.in0(in_2), .in1(in_6), .out(D3), .sel(a_b));
  Multiplexer #(.enable("false")) multiplexer_2 (.in0(in_3), .in1(in_7), .out(D2), .sel(a_b));
  Multiplexer #(.enable("false")) multiplexer_3 (.in0(in_4), .in1(in_8), .out(D1), .sel(a_b));
  Multiplexer #(.enable("false")) multiplexer_4 (.in0(in_5), .in1(in_9), .out(D0), .sel(a_b));
  and and_2 (and_2_out, in_1, D1);
  Multiplexer #(.enable("false")) multiplexer_5 (.in0(S0), .in1(j_k_ff_1_qn), .out(multiplexer_5_out), .sel(not_2_out));
  not not_1 (not_1_out, a_b);
  not not_2 (not_2_out, LM);
  J_K_Flip_Flop #(.enable("true")) j_k_ff_2 (
    .J(Ena), .clk(multiplexer_5_out), .K(Ena), .Q(S1), .Qn(j_k_ff_2_qn), .preset(and_2_out), .en(Ena),
    .reset(in_10));
  Multiplexer #(.enable("false")) multiplexer_6 (.in0(in_2), .in1(in_6), .out(U3), .sel(not_1_out));
  Multiplexer #(.enable("false")) multiplexer_7 (.in0(in_3), .in1(in_7), .out(U2), .sel(not_1_out));
  Multiplexer #(.enable("false")) multiplexer_8 (.in0(in_4), .in1(in_8), .out(U1), .sel(not_1_out));
  Multiplexer #(.enable("false")) multiplexer_9 (.in0(in_5), .in1(in_9), .out(U0), .sel(not_1_out));
  and and_3 (and_3_out, in_1, D2);
  Multiplexer #(.enable("false")) multiplexer_10 (
    .in0(S1), .in1(j_k_ff_2_qn), .out(multiplexer_10_out), .sel(not_2_out));
  J_K_Flip_Flop #(.enable("true")) j_k_ff_3 (
    .J(Ena), .clk(multiplexer_10_out), .K(Ena), .Q(S2), .Qn(j_k_ff_3_qn), .preset(and_3_out), .en(Ena),
    .reset(in_10));
  and and_4 (and_4_out, in_1, D3);
  Multiplexer #(.enable("false")) multiplexer_11 (
    .in0(S2), .in1(j_k_ff_3_qn), .out(multiplexer_11_out), .sel(not_2_out));
  J_K_Flip_Flop #(.enable("true")) j_k_ff_4 (
    .J(Ena), .clk(multiplexer_11_out), .K(Ena), .Q(S3), .Qn(j_k_ff_4_qn), .preset(and_4_out), .en(Ena),
    .reset(in_10));
  Comparator #(.width(4), .mode("unsigned")) comparator_2 (
    .a({S3, S2, S1, S0}), .b({U3, U2, U1, U0}), .eq(comparator_2_eq));  // open: gt, lt
  Comparator #(.width(4), .mode("unsigned")) comparator_3 (
    .a({S3, S2, S1, S0}), .b({D3, D2, D1, D0}), .eq(comparator_3_eq));  // open: gt, lt
  _7_Segment_Display u_7_segment_display_1 (.g(DG1), .f(DF1), .a(DA1), .b(DB1), .e(DE1), .d(DD1), .c(DC1), .dp(1'b0));
  _7447 #(.ShowInternalStructure("true")) u_7447_1 (
    .pin1(S1), .pin2(S2), .pin6(S3), .pin7(S0), .pin15(DF1), .pin14(DG1), .pin13(DA1), .pin12(DB1),
    .pin11(DC1), .pin10(DD1), .pin9(DE1));  // open: pin3, pin4, pin5
  xor xor_1 (xor_1_out, comparator_2_eq, comparator_3_eq);
  D_Flip_Flop d_ff_1 (.clk(CLK), .D(xor_1_out), .Q(d_ff_1_q));  // open: Qn, preset, reset
  J_K_Flip_Flop j_k_ff_5 (.J(d_ff_1_q), .clk(CLK), .K(d_ff_1_q), .Qn(LM));  // open: Q, preset, reset

  // Other names for the same wires on the sheet: A0 = in_5; A1 = in_4; A2 = in_3; A3 = in_2; B0 = in_9; B1 = in_8;
  //   B2 = in_7; B3 = in_6; LD = in_1; PW = Ena

  // Notes on the sheet:
  //   A > B
  //   B > A
  //   Menor Valor
  //   Maior Valor
  //   A > B
  //   B > A
  //   A > B
  //   B > A
endmodule
