// Logisim project LAB08.circ as structural Verilog: 7 circuits, main circuit main
module main (
  input  EN,
  input  CLR,
  input  in_3,
  input  in_4,
  input  in_5,
  input  in_6
);

  wire add_1_out_5, add_1_out_6, add_1_out_7, add_1_out_8, ADDSUB0, ADDSUB1, ADDSUB2, ADDSUB3, CLK, DA1, DB1,
       DC1, DD1, DE1, DF1, DG1, INPUT, not_1_out, not_2_out, not_3_out, not_4_out, not_5_out, S_LI, S_LI_t,
       S_LI_t_t, S_LM, STD, sub_1_out_5, sub_1_out_6, sub_1_out_7, sub_1_out_8, UN0, UN1, UN2, UN3;

  Clock u_CLK (.out(CLK));
  not not_1 (not_1_out, ADDSUB0);
  _7447 u_7447_1 (
    .pin1(UN1), .pin2(UN2), .pin6(UN3), .pin7(UN0), .pin15(DF1), .pin14(DG1), .pin13(DA1), .pin12(DB1),
    .pin11(DC1), .pin10(DD1), .pin9(DE1));  // open: pin3, pin4, pin5
  J_K_Flip_Flop #(.enable("true")) j_k_ff_1 (
    .J(ADDSUB0), .clk(CLK), .K(not_1_out), .Q(UN0), .en(EN), .reset(CLR));  // open: Qn, preset
  not not_2 (not_2_out, ADDSUB1);
  COMP comp_1 (
    .LSB(UN0), .in_2(UN1), .in_3(UN2), .in_4(UN3), .LSB_2(in_6), .in_6(in_5), .in_7(in_4), .in_8(in_3),
    .out_10(S_LM));  // open: out_9, out_11
  _7_Segment_Display u_7_segment_display_1 (.g(DG1), .f(DF1), .a(DA1), .b(DB1), .e(DE1), .d(DD1), .c(DC1), .dp(1'b0));
  J_K_Flip_Flop #(.enable("true")) j_k_ff_2 (
    .J(ADDSUB1), .clk(CLK), .K(not_2_out), .Q(UN1), .en(EN), .reset(CLR));  // open: Qn, preset
  COMP comp_2 (
    .LSB(UN0), .in_2(UN1), .in_3(UN2), .in_4(UN3), .LSB_2(1'b0), .in_6(1'b0), .in_7(1'b0), .in_8(1'b0),
    .out_10(S_LI_t), .out_9(S_LI_t_t), .out_11(S_LI));
  not not_3 (not_3_out, ADDSUB2);
  J_K_Flip_Flop #(.enable("true")) j_k_ff_3 (
    .J(ADDSUB2), .clk(CLK), .K(not_3_out), .Q(UN2), .en(EN), .reset(CLR));  // open: Qn, preset
  J_K_Flip_Flop #(.enable("true")) j_k_ff_4 (
    .J(INPUT), .clk(CLK), .K(not_4_out), .Q(STD), .en(EN));  // open: Qn, preset, reset
  not not_4 (not_4_out, INPUT);
  ADD add_1 (
    .in_1(UN0), .in_2(UN1), .in_3(UN2), .in_4(UN3), .out_5(add_1_out_5), .out_6(add_1_out_6),
    .out_7(add_1_out_7), .out_8(add_1_out_8));
  MUX8x4 mux8x4_1 (
    .in_1(add_1_out_5), .in_2(sub_1_out_5), .in_3(add_1_out_6), .in_4(sub_1_out_6), .in_5(add_1_out_7),
    .in_6(sub_1_out_7), .in_7(add_1_out_8), .in_8(sub_1_out_8), .out_10(ADDSUB0), .out_11(ADDSUB1),
    .out_12(ADDSUB2), .out_13(ADDSUB3), .in_9(INPUT));
  SUB sub_1 (
    .in_1(UN0), .in_2(UN1), .in_3(UN2), .in_4(UN3), .out_5(sub_1_out_5), .out_6(sub_1_out_6),
    .out_7(sub_1_out_7), .out_8(sub_1_out_8));
  not not_5 (not_5_out, ADDSUB3);
  J_K_Flip_Flop #(.enable("true")) j_k_ff_5 (
    .J(ADDSUB3), .clk(CLK), .K(not_5_out), .Q(UN3), .en(EN), .reset(CLR));  // open: Qn, preset
  CE ce_1 (.LMS(S_LM), .LMI(S_LI_t), .STDA(STD), .INPUT(INPUT));

  // Other names for the same wires on the sheet: B0 = in_6; B1 = in_5; B2 = in_4; B3 = in_3

  // Notes on the sheet:
  //   COMP A
  //   COMP 0
  //   CONTADOR SINCRONO
  //   ADD and SUB 
  //   CONTROLE DE ESTADO
endmodule

module MDE (
  input  EN,
  input  UD,
  input  STPUQ,
  input  STPDQ,
  input  COMPQ,
  output STPDD,
  output STPUD,
  output UDD
);

  wire and_2_out, not_1_out;

  not not_1 (not_1_out, UD);
  and and_1 (STPUD, UD, COMPQ);
  and and_2 (and_2_out, UD, COMPQ);
  and and_3 (STPDD, not_1_out, COMPQ);
  or or_1 (UDD, STPDQ, and_2_out);
endmodule

module MUX8x4 (
  input  in_1,
  input  in_2,
  input  in_3,
  input  in_4,
  input  in_5,
  input  in_6,
  input  in_7,
  input  in_8,
  input  in_9,
  output out_10,
  output out_11,
  output out_12,
  output out_13
);

  Multiplexer #(.enable("false")) multiplexer_1 (.in0(in_1), .in1(in_2), .out(out_10), .sel(in_9));
  Multiplexer #(.enable("false")) multiplexer_2 (.in0(in_3), .in1(in_4), .out(out_11), .sel(in_9));
  Multiplexer #(.enable("false")) multiplexer_3 (.in0(in_5), .in1(in_6), .out(out_12), .sel(in_9));
  Multiplexer #(.enable("false")) multiplexer_4 (.in0(in_7), .in1(in_8), .out(out_13), .sel(in_9));
endmodule

module ADD (
  input  in_1,
  input  in_2,
  input  in_3,
  input  in_4,
  output out_5,
  output out_6,
  output out_7,
  output out_8
);

  Adder #(.width(4)) adder_1 (
    .a({in_4, in_3, in_2, in_1}), .b(4'b0001), .out({out_8, out_7, out_6, out_5}), .cin(1'b0));  // open: cout
endmodule

module SUB (
  input  in_1,
  input  in_2,
  input  in_3,
  input  in_4,
  output out_5,
  output out_6,
  output out_7,
  output out_8
);

  Subtractor #(.width(4)) subtractor_1 (
    .a({in_4, in_3, in_2, in_1}), .b(4'b0001), .out({out_8, out_7, out_6, out_5}), .bin(1'b0));  // open: bout
endmodule

module COMP (
  input  LSB,
  input  in_2,
  input  in_3,
  input  in_4,
  input  LSB_2,
  input  in_6,
  input  in_7,
  input  in_8,
  output out_9,
  output out_10,
  output out_11
);

  Comparator #(.width(4), .mode("unsigned")) comparator_1 (
    .a({in_4, in_3, in_2, LSB}), .b({in_8, in_7, in_6, LSB_2}), .gt(out_9), .eq(out_10), .lt(out_11));
endmodule

module CE (
  input  LMS,
  input  LMI,
  input  STDA,
  output INPUT
);

  wire and_1_out, and_2_out, not_1_out, not_2_out;

  not not_1 (not_1_out, LMI);
  not not_2 (not_2_out, LMI);
  and and_1 (and_1_out, not_1_out, STDA);
  and and_2 (and_2_out, LMS, not_2_out);
  or or_1 (INPUT, and_1_out, and_2_out);
endmodule
