// Logisim project LAB09.circ as structural Verilog: 2 circuits, main circuit main
module main (
  input  CLR,
  input  U,
  input  Y,
  output out_4,
  output out_5,
  output Z
);

  wire clock_1_out, D0, D1, Q0, Q1;

  Clock clock_1 (.out(clock_1_out));
  MDE mde_1 (.CLR(CLR), .Q1(Q1), .Q0(Q0), .U(U), .Y(Y), .D1(D1), .D0(D0), .E1(out_4), .E0(out_5), .Z(Z));
  D_Flip_Flop d_ff_1 (.clk(clock_1_out), .D(D0), .Q(Q0));  // open: Qn, preset, reset
  D_Flip_Flop d_ff_2 (.clk(clock_1_out), .D(D1), .Q(Q1));  // open: Qn, preset, reset
endmodule

module MDE (
  input  CLR,
  input  Q1,
  input  Q0,
  input  U,
  input  Y,
  output D1,
  output D0,
  output E1,
  output E0,
  output Z
);

  wire and_1_out, and_2_out, and_3_out, and_4_out, and_5_out, and_6_out, and_7_out, and_10_out, and_11_out,
       not_1_out, not_2_out, not_3_out, not_4_out, not_5_out, not_6_out, not_7_out, not_8_out, not_9_out,
       not_10_out, not_11_out, not_12_out, not_13_out, not_14_out, not_15_out, not_16_out, not_17_out,
       not_18_out, not_19_out, not_20_out, not_21_out, not_22_out, not_23_out;

  not not_1 (not_1_out, CLR);
  not not_2 (not_2_out, Q1);
  not not_3 (not_3_out, Q0);
  not not_4 (not_4_out, U);
  not not_5 (not_5_out, Y);
  not not_6 (not_6_out, CLR);
  not not_7 (not_7_out, Q1);
  not not_8 (not_8_out, U);
  not not_9 (not_9_out, CLR);
  not not_10 (not_10_out, Q0);
  not not_11 (not_11_out, CLR);
  not not_12 (not_12_out, CLR);
  not not_13 (not_13_out, Y);
  not not_14 (not_14_out, CLR);
  not not_15 (not_15_out, Q0);
  not not_16 (not_16_out, U);
  not not_17 (not_17_out, CLR);
  not not_18 (not_18_out, CLR);
  not not_19 (not_19_out, CLR);
  not not_20 (not_20_out, CLR);
  not not_21 (not_21_out, CLR);
  not not_22 (not_22_out, Q0);
  not not_23 (not_23_out, Y);
  and and_1 (and_1_out, not_1_out, not_2_out, not_3_out, not_4_out, not_5_out);
  and and_2 (and_2_out, not_6_out, not_7_out, Q0, not_8_out, Y);
  and and_3 (and_3_out, not_9_out, Q1, not_10_out, Y);
  and and_4 (and_4_out, not_11_out, Q1, U);
  and and_5 (and_5_out, not_12_out, Q1, Q0, not_13_out);
  and and_6 (and_6_out, not_14_out, not_15_out, not_16_out);
  and and_7 (and_7_out, not_17_out, Q0, U);
  and and_8 (E1, not_18_out, Q1);
  and and_9 (E0, not_19_out, Q0);
  and and_10 (and_10_out, not_20_out, U);
  and and_11 (and_11_out, not_21_out, Q1, not_22_out, not_23_out);
  or or_1 (D1, and_1_out, and_2_out, and_3_out, and_4_out, and_5_out);
  or or_2 (D0, and_6_out, and_7_out);
  or or_3 (Z, and_10_out, and_11_out);
endmodule
