// Logisim project LAB10.circ as structural Verilog: 3 circuits, main circuit main
module main (
  input  in_1,
  input  in_2,
  input  in_3,
  input  in_4
);

  wire CLK, CLR, LOAD, multiplexer_1_out, multiplexer_2_out, multiplexer_3_out, multiplexer_4_out, S0, S1,
       S2, S3, SET, SHL, SHL_IN, SHR, SHR_IN;
  wire [2:0] ST;

  // DipSwitch #(.NSwitches(5)) dipswitch_1: pin names not known; wires that end beside it: CLR, LOAD, SHR, SHL, SET
  Multiplexer #(.select(3), .enable("false")) multiplexer_1 (
    .in0(S0), .in1(1'b1), .in2(S1), .in3(SHR_IN), .in4(in_1), .in5(1'b0), .in6(1'b0), .in7(1'b0),
    .out(multiplexer_1_out), .sel(ST));
  Multiplexer #(.select(3), .enable("false")) multiplexer_2 (
    .in0(S2), .in1(1'b1), .in2(S3), .in3(S1), .in4(in_3), .in5(1'b0), .in6(1'b0), .in7(1'b0),
    .out(multiplexer_2_out), .sel(ST));
  Clock clock_1 (.out(CLK));
  Button button_1 (.out(SHR_IN));
  Button button_2 (.out(SHL_IN));
  LED led_1 (.in(S0));
  LED led_2 (.in(S1));
  D_Flip_Flop d_ff_1 (.clk(CLK), .D(multiplexer_1_out), .Q(S0), .reset(CLR));  // open: Qn, preset
  D_Flip_Flop d_ff_2 (.clk(CLK), .D(multiplexer_2_out), .Q(S2), .reset(CLR));  // open: Qn, preset
  LED led_3 (.in(S2));
  LED led_4 (.in(S3));
  Multiplexer #(.select(3), .enable("false")) multiplexer_3 (
    .in0(S1), .in1(1'b1), .in2(S2), .in3(S0), .in4(in_2), .in5(1'b0), .in6(1'b0), .in7(1'b0),
    .out(multiplexer_3_out), .sel(ST));
  Multiplexer #(.select(3), .enable("false")) multiplexer_4 (
    .in0(S3), .in1(1'b1), .in2(SHL_IN), .in3(S2), .in4(in_4), .in5(1'b0), .in6(1'b0), .in7(1'b0),
    .out(multiplexer_4_out), .sel(ST));
  \Controle_De_Funçao  \controle_de_funçao_1  (
    .LOAD(LOAD), .S2(ST[2]), .SHR(SHR), .S1(ST[1]), .SHL(SHL), .SET(SET), .S0(ST[0]));
  D_Flip_Flop d_ff_3 (.clk(CLK), .D(multiplexer_3_out), .Q(S1), .reset(CLR));  // open: Qn, preset
  D_Flip_Flop d_ff_4 (.clk(CLK), .D(multiplexer_4_out), .Q(S3), .reset(CLR));  // open: Qn, preset

  // Other names for the same wires on the sheet: B0 = in_1; B1 = in_2; B2 = in_3; B3 = in_4
endmodule

module \Controle_De_Funçao  (
  input  LOAD,
  input  SHR,
  input  SHL,
  input  SET,
  output S2,
  output S1,
  output S0
);

  wire and_1_out, and_2_out, and_3_out, and_4_out, not_1_out, not_2_out, not_3_out, not_4_out, not_5_out;

  not not_1 (not_1_out, LOAD);
  and and_1 (and_1_out, not_1_out, SHL);
  not not_2 (not_2_out, LOAD);
  and and_2 (and_2_out, not_2_out, SHR);
  not not_3 (not_3_out, LOAD);
  not not_4 (not_4_out, SHL);
  and and_3 (and_3_out, not_3_out, not_4_out, SET);
  not not_5 (not_5_out, LOAD);
  and and_4 (and_4_out, not_5_out, SHR);
  or or_1 (S1, and_1_out, and_2_out);
  or or_2 (S0, and_3_out, and_4_out);

  assign S2 = LOAD;
endmodule

module TESTE (
  input  in_1,
  input  in_2,
  input  in_3,
  input  in_4,
  input  in_5,
  input  in_6,
  output out_7,
  output out_8,
  output out_9,
  output out_10
);

  wire CLK, N0, N1, N2, N3, not_1_out;

  D_Flip_Flop d_ff_1 (.clk(CLK), .D(N0), .Q(out_7));  // open: Qn, preset, reset
  D_Flip_Flop d_ff_2 (.clk(CLK), .D(N2), .Q(out_9));  // open: Qn, preset, reset
  Clock clock_1 (.out(CLK));
  D_Flip_Flop d_ff_3 (.clk(CLK), .D(N1), .Q(out_8));  // open: Qn, preset, reset
  D_Flip_Flop d_ff_4 (.clk(CLK), .D(N3), .Q(out_10));  // open: Qn, preset, reset
  not not_1 (not_1_out, in_6);
  Multiplexer #(.enable("false")) multiplexer_1 (.in0(in_5), .in1(out_7), .out(N0), .sel(not_1_out));
  Multiplexer #(.enable("false")) multiplexer_2 (.in0(out_7), .in1(out_8), .out(N1), .sel(not_1_out));
  Multiplexer #(.enable("false")) multiplexer_3 (.in0(out_8), .in1(out_9), .out(N2), .sel(not_1_out));
  Multiplexer #(.enable("false")) multiplexer_4 (.in0(out_9), .in1(out_10), .out(N3), .sel(not_1_out));
  Multiplexer #(.enable("false")) multiplexer_5 (.in0(out_10), .in1(1'b0), .sel(not_1_out));  // open: out

  // Other names for the same wires on the sheet: B0 = in_1; B1 = in_2; B2 = in_3; B3 = in_4; DB0 = out_7; DB1 = out_8;
  //   DB2 = out_9; DB3 = out_10; S2 = N2; SHR = in_6; SHR_IN = in_5
endmodule
