// Logisim project LAB11.circ as structural Verilog: 4 circuits, main circuit main
module main (
  input  in_1,
  input  in_2,
  input  in_3,
  input  in_4,
  input  in_5,
  input  in_6,
  input  in_7,
  input  in_8,
  input  in_9
);

  wire bloco_de_controle_1_cl, bloco_de_controle_1_d, bloco_de_controle_1_ld, bloco_operacional_1_out_12,
       clock_1_out;

  Clock clock_1 (.out(clock_1_out));
  Bloco_de_Controle bloco_de_controle_1 (
    .ME(bloco_operacional_1_out_12), .C(in_9), .CLK(clock_1_out), .ld(bloco_de_controle_1_ld),
    .cl(bloco_de_controle_1_cl), .d(bloco_de_controle_1_d));
  LED led_1 (.in(bloco_de_controle_1_d));
  Bloco_Operacional bloco_operacional_1 (
    .out_12(bloco_operacional_1_out_12), .in_8(in_1), .in_9(in_2), .in_10(in_3), .in_11(in_4),
    .clk(clock_1_out), .ld(bloco_de_controle_1_ld), .zero(bloco_de_controle_1_cl), .in_2(in_5), .in_3(in_6),
    .in_4(in_7), .in_5(in_8));
endmodule

module Bloco_Operacional (
  input  clk,
  input  in_2,
  input  in_3,
  input  in_4,
  input  in_5,
  input  ld,
  input  zero,
  input  in_8,
  input  in_9,
  input  in_10,
  input  in_11,
  output out_12
);

  wire [3:0] _1, register_1_q;

  Register #(.width(4), .Select("low")) register_1 (.D(_1), .en(ld), .Q(register_1_q), .clk(clk), .clr(zero));
  Adder #(.width(4)) adder_1 (.a({in_2, in_3, in_4, in_5}), .b(register_1_q), .out(_1));  // open: cin, cout
  Comparator #(.width(4), .mode("unsigned")) comparator_1 (
    .a({in_8, in_9, in_10, in_11}), .b(register_1_q), .lt(out_12));  // open: gt, eq
endmodule

module MLL (
  input  Q1,
  input  Q0,
  input  ME,
  input  C,
  output D1,
  output D0,
  output LD,
  output CL,
  output D
);

  wire and_2_out, and_3_out, and_4_out, and_5_out, not_1_out, not_2_out, not_3_out, not_4_out, not_5_out,
       not_6_out, not_7_out, not_8_out;

  not not_1 (not_1_out, Q1);
  and and_1 (D1, not_1_out, Q0);
  not not_2 (not_2_out, Q1);
  not not_3 (not_3_out, Q0);
  and and_2 (and_2_out, not_2_out, not_3_out, C);
  not not_4 (not_4_out, Q1);
  and and_3 (and_3_out, not_4_out, Q0, not_5_out);
  not not_5 (not_5_out, ME);
  not not_6 (not_6_out, Q1);
  and and_4 (and_4_out, not_6_out, C);
  not not_7 (not_7_out, Q1);
  and and_5 (and_5_out, not_7_out, Q0);
  and and_6 (CL, Q1, Q0);
  and and_7 (D, Q1, not_8_out);
  not not_8 (not_8_out, Q0);
  or or_1 (D0, and_2_out, and_3_out);
  or or_2 (LD, and_4_out, and_5_out);
endmodule

module Bloco_de_Controle (
  input  ME,
  input  C,
  input  CLK,
  output ld,
  output cl,
  output d
);

  wire D0, D1, Q0, Q1;

  MLL mll_1 (.Q1(Q1), .Q0(Q0), .ME(ME), .C(C), .D1(D1), .D0(D0), .LD(ld), .CL(cl), .D(d));
  D_Flip_Flop d_ff_1 (.clk(CLK), .D(D1), .Q(Q1));  // open: Qn, preset, reset
  D_Flip_Flop d_ff_2 (.clk(CLK), .D(D0), .Q(Q0));  // open: Qn, preset, reset
endmodule
