// Logisim project Operaçoes.circ as structural Verilog
module REG11Bits (
  input  in_1,
  input  in_2,
  input  in_3,
  input  in_4,
  input  in_5,
  input  in_6,
  input  in_7,
  input  in_8,
  input  in_9,
  input  in_10,
  input  in_11,
  input  CLK,
  input  EN,
  input  _0,
  output out_15,
  output out_16,
  output out_17,
  output out_18,
  output out_19,
  output out_20,
  output out_21,
  output out_22,
  output out_23,
  output out_24,
  output out_25
);

  Register #(.width(11), .Select("low")) register_1 (
    .D({in_11, in_10, in_9, in_8, in_7, in_6, in_5, in_4, in_3, in_2, in_1}), .en(EN),
    .Q({out_25, out_24, out_23, out_22, out_21, out_20, out_19, out_18, out_17, out_16, out_15}), .clk(CLK),
    .clr(_0));
endmodule

module COMP11Bits (
  input  in_1,
  input  in_2,
  input  in_3,
  input  in_4,
  input  in_5,
  input  in_6,
  input  in_7,
  input  in_8,
  input  in_9,
  input  in_10,
  input  in_11,
  input  in_12,
  input  in_13,
  input  in_14,
  input  in_15,
  input  in_16,
  input  in_17,
  input  in_18,
  input  in_19,
  input  in_20,
  input  in_21,
  input  in_22,
  output out_23,
  output out_24,
  output out_25
);

  Comparator #(.width(11), .mode("unsigned")) comparator_1 (
    .a({in_22, in_20, in_18, in_16, in_14, in_12, in_10, in_8, in_6, in_4, in_2}),
    .b({in_21, in_19, in_17, in_15, in_13, in_11, in_9, in_7, in_5, in_3, in_1}), .gt(out_23), .eq(out_24),
    .lt(out_25));
endmodule

module SUM11Bits (
  input  in_1,
  input  in_2,
  input  in_3,
  input  in_4,
  input  in_5,
  input  in_6,
  input  in_7,
  input  in_8,
  input  in_9,
  input  in_10,
  input  in_11,
  input  in_12,
  input  in_13,
  input  in_14,
  input  in_15,
  input  in_16,
  input  in_17,
  input  in_18,
  input  in_19,
  input  in_20,
  input  in_21,
  input  in_22,
  input  in_23,
  output out_24,
  output out_25,
  output out_26,
  output out_27,
  output out_28,
  output out_29,
  output out_30,
  output out_31,
  output out_32,
  output out_33,
  output out_34
);

  Adder #(.width(11)) adder_1 (
    .a({in_12, in_11, in_10, in_9, in_8, in_7, in_5, in_4, in_3, in_2, in_1}),
    .b({in_23, in_22, in_21, in_20, in_19, in_18, in_17, in_16, in_15, in_14, in_13}),
    .out({out_34, out_33, out_32, out_31, out_30, out_29, out_28, out_27, out_26, out_25, out_24}), .cin(in_6));  // open: cout
endmodule

module SUM_COMP (
  input  [10:0] COMP,
  input  [10:0] A,
  input  [10:0] B,
  output out_4,
  output out_5,
  output out_6
);

  wire sum11bits_1_out_24, sum11bits_1_out_25, sum11bits_1_out_26, sum11bits_1_out_27, sum11bits_1_out_28,
       sum11bits_1_out_29, sum11bits_1_out_30, sum11bits_1_out_31, sum11bits_1_out_32, sum11bits_1_out_33,
       sum11bits_1_out_34;

  SUM11Bits sum11bits_1 (
    .in_1(A[0]), .in_2(A[1]), .in_3(A[2]), .in_4(A[3]), .in_5(A[4]), .in_7(A[5]), .in_8(A[6]), .in_9(A[7]),
    .in_10(A[8]), .in_11(A[9]), .in_12(A[10]), .in_13(B[0]), .in_14(B[1]), .in_15(B[2]), .in_16(B[3]),
    .in_17(B[4]), .in_18(B[5]), .in_19(B[6]), .in_20(B[7]), .in_21(B[8]), .in_22(B[9]), .in_23(B[10]),
    .out_24(sum11bits_1_out_24), .out_25(sum11bits_1_out_25), .out_26(sum11bits_1_out_26),
    .out_27(sum11bits_1_out_27), .out_28(sum11bits_1_out_28), .out_29(sum11bits_1_out_29),
    .out_30(sum11bits_1_out_30), .out_31(sum11bits_1_out_31), .out_32(sum11bits_1_out_32),
    .out_33(sum11bits_1_out_33), .out_34(sum11bits_1_out_34));  // open: in_6
  COMP11Bits comp11bits_1 (
    .in_2(COMP[0]), .in_4(COMP[1]), .in_6(COMP[2]), .in_8(COMP[3]), .in_10(COMP[4]), .in_12(COMP[5]),
    .in_14(COMP[6]), .in_16(COMP[7]), .in_18(COMP[8]), .in_20(COMP[9]), .in_22(COMP[10]), .out_24(out_5),
    .in_1(sum11bits_1_out_24), .in_3(sum11bits_1_out_25), .in_5(sum11bits_1_out_26),
    .in_7(sum11bits_1_out_27), .in_9(sum11bits_1_out_28), .in_11(sum11bits_1_out_29),
    .in_13(sum11bits_1_out_30), .in_15(sum11bits_1_out_31), .in_17(sum11bits_1_out_32),
    .in_19(sum11bits_1_out_33), .in_21(sum11bits_1_out_34), .out_23(out_6), .out_25(out_4));
endmodule

module SUM_REG (
  input  CLK,
  input  EN,
  input  _0,
  input  [10:0] B,
  output [10:0] REGISTER
);

  wire sum11bits_1_out_24, sum11bits_1_out_25, sum11bits_1_out_26, sum11bits_1_out_27, sum11bits_1_out_28,
       sum11bits_1_out_29, sum11bits_1_out_30, sum11bits_1_out_31, sum11bits_1_out_32, sum11bits_1_out_33,
       sum11bits_1_out_34;

  REG11Bits reg11bits_1 (
    .CLK(CLK), .EN(EN), .in_1(sum11bits_1_out_24), .in_2(sum11bits_1_out_25), .in_3(sum11bits_1_out_26),
    .in_4(sum11bits_1_out_27), .in_5(sum11bits_1_out_28), .in_6(sum11bits_1_out_29),
    .in_7(sum11bits_1_out_30), .in_8(sum11bits_1_out_31), .in_9(sum11bits_1_out_32),
    .in_10(sum11bits_1_out_33), .in_11(sum11bits_1_out_34), .out_15(REGISTER[0]), .out_16(REGISTER[1]),
    .out_17(REGISTER[2]), .out_18(REGISTER[3]), .out_19(REGISTER[4]), .out_20(REGISTER[5]),
    .out_21(REGISTER[6]), .out_22(REGISTER[7]), .out_23(REGISTER[8]), .out_24(REGISTER[9]),
    .out_25(REGISTER[10]), ._0(_0));
  SUM11Bits sum11bits_1 (
    .in_1(REGISTER[0]), .in_2(REGISTER[1]), .in_3(REGISTER[2]), .in_4(REGISTER[3]), .in_5(REGISTER[4]),
    .in_7(REGISTER[5]), .in_8(REGISTER[6]), .in_9(REGISTER[7]), .in_10(REGISTER[8]), .in_11(REGISTER[9]),
    .in_12(REGISTER[10]), .in_13(B[0]), .in_14(B[1]), .in_15(B[2]), .in_16(B[3]), .in_17(B[4]), .in_18(B[5]),
    .in_19(B[6]), .in_20(B[7]), .in_21(B[8]), .in_22(B[9]), .in_23(B[10]), .out_24(sum11bits_1_out_24),
    .out_25(sum11bits_1_out_25), .out_26(sum11bits_1_out_26), .out_27(sum11bits_1_out_27),
    .out_28(sum11bits_1_out_28), .out_29(sum11bits_1_out_29), .out_30(sum11bits_1_out_30),
    .out_31(sum11bits_1_out_31), .out_32(sum11bits_1_out_32), .out_33(sum11bits_1_out_33),
    .out_34(sum11bits_1_out_34));  // open: in_6

  // Other names for the same wires on the sheet: RELOAD[10:0] = REGISTER
endmodule

module Button (
  input  Q1,
  input  Q0,
  input  T,
  output D1,
  output D0,
  output PRESS
);

  wire and_1_out, and_2_out, CLK, not_1_out, not_2_out, not_3_out, not_4_out, not_5_out, Q0_t, Q1_t;

  not not_1 (not_1_out, Q1);
  not not_2 (not_2_out, Q0);
  not not_3 (not_3_out, Q1);
  not not_4 (not_4_out, Q0);
  not not_5 (not_5_out, Q1);
  and and_1 (and_1_out, not_1_out, Q0);
  and and_2 (and_2_out, Q1, not_2_out, T);
  and and_3 (D0, not_3_out, not_4_out, T);
  and and_4 (PRESS, not_5_out, Q0);
  D_Flip_Flop d_ff_1 (.clk(CLK), .D(D0), .Q(Q0_t));  // open: Qn, preset, reset
  D_Flip_Flop d_ff_2 (.clk(CLK), .D(D1), .Q(Q1_t));  // open: Qn, preset, reset
  or or_1 (D1, and_1_out, and_2_out);
endmodule
