// Logisim project TEO04.circ as structural Verilog
module Soma (
  input  CI,
  input  A,
  input  B,
  output CO,
  output S
);

  wire and_1_out, and_2_out, and_3_out;

  and and_1 (and_1_out, A, B);
  and and_2 (and_2_out, A, CI);
  and and_3 (and_3_out, B, CI);
  or or_1 (CO, and_1_out, and_2_out, and_3_out);
  xor xor_1 (S, CI, A, B);

  // Other names for the same wires on the sheet: c = CI
endmodule

module STRUCT_SOMA (
  input  in_1,
  input  in_2,
  input  in_3,
  input  in_4,
  input  in_5,
  input  in_6,
  input  in_7,
  input  in_8,
  input  in_9,
  input  in_10,
  input  in_11,
  input  in_12,
  input  in_13,
  input  in_14,
  input  in_15,
  input  in_16,
  input  in_17,
  output out_18,
  output out_19,
  output out_20,
  output out_21,
  output out_22,
  output out_23,
  output out_24,
  output out_25,
  output out_26
);

  wire soma_1_co, soma_2_co, soma_3_co, soma_4_co, soma_5_co, soma_6_co, soma_7_co;

  Soma soma_1 (.CI(in_9), .A(in_1), .B(in_10), .CO(soma_1_co), .S(out_18));
  Soma soma_2 (.CI(soma_1_co), .A(in_2), .B(in_11), .CO(soma_2_co), .S(out_19));
  Soma soma_3 (.CI(soma_2_co), .A(in_3), .B(in_12), .CO(soma_3_co), .S(out_20));
  Soma soma_4 (.CI(soma_3_co), .A(in_4), .B(in_13), .CO(soma_4_co), .S(out_21));
  Soma soma_5 (.CI(soma_4_co), .A(in_5), .B(in_14), .CO(soma_5_co), .S(out_22));
  Soma soma_6 (.CI(soma_5_co), .A(in_6), .B(in_15), .CO(soma_6_co), .S(out_23));
  Soma soma_7 (.CI(soma_6_co), .A(in_7), .B(in_16), .CO(soma_7_co), .S(out_24));
  Soma soma_8 (.CI(soma_7_co), .A(in_8), .B(in_17), .CO(out_26), .S(out_25));
endmodule

module OP_SOMA (
  input  in_1,
  input  in_2,
  input  in_3,
  input  in_4,
  input  in_5,
  input  in_6,
  input  in_7,
  input  in_8,
  input  in_9,
  input  in_10,
  input  in_11,
  input  in_12,
  input  in_13,
  input  in_14,
  input  in_15,
  input  in_16,
  input  in_17,
  output out_18,
  output out_19,
  output out_20,
  output out_21,
  output out_22,
  output out_23,
  output out_24,
  output out_25
);

  STRUCT_SOMA struct_soma_1 (
    .in_9(in_17), .in_1(in_8), .in_10(in_16), .in_2(in_7), .in_11(in_15), .in_3(in_6), .in_12(in_14),
    .in_4(in_5), .in_13(in_13), .in_5(in_4), .in_14(in_12), .in_6(in_3), .in_15(in_11), .in_7(in_2),
    .in_16(in_10), .in_8(in_1), .in_17(in_9), .out_18(out_25), .out_20(out_23), .out_21(out_22),
    .out_22(out_21), .out_23(out_20), .out_24(out_19), .out_25(out_18), .out_19(out_24));  // open: out_26

  // Other names for the same wires on the sheet: A0 = in_8; A1 = in_7; A2 = in_6; A3 = in_5; A4 = in_4; A5 = in_3;
  //   A6 = in_2; A7 = in_1; B0 = in_16; B1 = in_15; B2 = in_14; B3 = in_13; B4 = in_12; B5 = in_11; B6 = in_10;
  //   B7 = in_9
endmodule

module OP_SUBTRATOR (
  input  in_1,
  input  in_2,
  input  in_3,
  input  in_4,
  input  in_5,
  input  in_6,
  input  in_7,
  input  in_8,
  input  in_9,
  input  in_10,
  input  in_11,
  input  in_12,
  input  in_13,
  input  in_14,
  input  in_15,
  input  in_16,
  output out_17,
  output out_18,
  output out_19,
  output out_20,
  output out_21,
  output out_22,
  output out_23,
  output out_24,
  output out_25
);

  wire B0, B1, B2, B3, B4, B5, B6, B7;

  STRUCT_SOMA struct_soma_1 (
    .in_9(1'b1), .in_1(in_8), .in_10(B0), .in_2(in_7), .in_11(B1), .in_3(in_6), .in_12(B2), .in_4(in_5),
    .in_13(B3), .in_5(in_4), .in_14(B4), .in_6(in_3), .in_15(B5), .in_7(in_2), .in_16(B6), .in_8(in_1),
    .in_17(B7), .out_18(out_25), .out_20(out_23), .out_21(out_22), .out_22(out_21), .out_23(out_20),
    .out_24(out_19), .out_25(out_18), .out_26(out_17), .out_19(out_24));
  not not_1 (B6, in_10);
  not not_2 (B7, in_9);
  not not_3 (B3, in_13);
  not not_4 (B2, in_14);
  not not_5 (B5, in_11);
  not not_6 (B4, in_12);
  not not_7 (B1, in_15);
  not not_8 (B0, in_16);

  // Other names for the same wires on the sheet: A0 = in_8; A1 = in_7; A2 = in_6; A3 = in_5; A4 = in_4; A5 = in_3;
  //   A6 = in_2; A7 = in_1
endmodule

module OP_INCREMENTAR (
  input  in_1,
  input  in_2,
  input  in_3,
  input  in_4,
  input  in_5,
  input  in_6,
  input  in_7,
  input  in_8,
  output out_9,
  output out_10,
  output out_11,
  output out_12,
  output out_13,
  output out_14,
  output out_15,
  output out_16
);

  STRUCT_SOMA struct_soma_1 (
    .in_9(1'b1), .in_1(in_8), .in_10(1'b0), .in_2(in_7), .in_11(1'b0), .in_3(in_6), .in_12(1'b0),
    .in_4(in_5), .in_13(1'b0), .in_5(in_4), .in_14(1'b0), .in_6(in_3), .in_15(1'b0), .in_7(in_2),
    .in_16(1'b0), .in_8(in_1), .in_17(1'b0), .out_18(out_16), .out_20(out_14), .out_21(out_13),
    .out_22(out_12), .out_23(out_11), .out_24(out_10), .out_25(out_9), .out_19(out_15));  // open: out_26

  // Other names for the same wires on the sheet: A0 = in_8; A1 = in_7; A2 = in_6; A3 = in_5; A4 = in_4; A5 = in_3;
  //   A6 = in_2; A7 = in_1
endmodule

module OP_DECREMENTADOR (
  input  in_1,
  input  in_2,
  input  in_3,
  input  in_4,
  input  in_5,
  input  in_6,
  input  in_7,
  input  in_8,
  output out_9,
  output out_10,
  output out_11,
  output out_12,
  output out_13,
  output out_14,
  output out_15,
  output out_16,
  output out_17
);

  wire B0, B1, B2, B3, B4, B5, B6, B7;

  STRUCT_SOMA struct_soma_1 (
    .in_9(1'b1), .in_1(in_8), .in_10(B0), .in_2(in_7), .in_11(B1), .in_3(in_6), .in_12(B2), .in_4(in_5),
    .in_13(B3), .in_5(in_4), .in_14(B4), .in_6(in_3), .in_15(B5), .in_7(in_2), .in_16(B6), .in_8(in_1),
    .in_17(B7), .out_18(out_17), .out_20(out_15), .out_21(out_14), .out_22(out_13), .out_23(out_12),
    .out_24(out_11), .out_25(out_10), .out_26(out_9), .out_19(out_16));
  not not_1 (B6, 1'b0);
  not not_2 (B7, 1'b0);
  not not_3 (B4, 1'b0);
  not not_4 (B2, 1'b0);
  not not_5 (B5, 1'b0);
  not not_6 (B3, 1'b0);
  not not_7 (B1, 1'b0);
  not not_8 (B0, 1'b1);

  // Other names for the same wires on the sheet: A0 = in_8; A1 = in_7; A2 = in_6; A3 = in_5; A4 = in_4; A5 = in_3;
  //   A6 = in_2; A7 = in_1
endmodule
