// Logisim project TEO05.circ as structural Verilog: 7 circuits, main circuit main
module main (
  input  in_1,
  input  in_2,
  input  in_3,
  input  in_4,
  input  LOAD,
  input  in_6,
  input  in_7,
  input  in_8,
  input  in_9,
  input  in_10,
  input  in_11,
  input  in_12,
  input  in_13,
  input  in_14,
  input  in_15,
  input  in_16,
  input  in_17,
  input  in_18,
  input  in_19,
  input  in_20,
  input  in_21,
  input  in_22,
  input  in_23,
  output out_24,
  output out_25,
  output out_26,
  output out_27,
  output out_28,
  output out_29,
  output out_30,
  output out_31,
  output out_32,
  output out_33,
  output out_34,
  output out_35
);

  wire A, B, B0, B1, B2, B3, B4, B5, B6, B7, B8, B9, BD_sb, C, CL0, CL1, comp10bits_1_a_b,
       comp10bits_1_a_b_2, comp10bits_1_out_24, D, DA1, DA2, DA3, DB1, DB2, DB3, DC1, DC2, DC3, DD1, DD2,
       DD3, DE1, DE2, DE3, DF1, DF2, DF3, DG1, DG2, DG3, E, F, G, H, I, J, j_k_ff_1_qn, j_k_ff_2_qn,
       j_k_ff_3_qn, j_k_ff_4_qn, j_k_ff_5_qn, j_k_ff_6_qn, j_k_ff_7_qn, j_k_ff_8_qn, j_k_ff_9_qn,
       j_k_ff_10_q, LB0, LB1, LB2, LB3, LD, MA, MA_MI, MB, MC, MD, ME, MF, MG, MH, MI, MJ, multiplexer_6_out,
       multiplexer_7_out, multiplexer_13_out, multiplexer_14_out, multiplexer_15_out, multiplexer_16_out,
       multiplexer_17_out, multiplexer_18_out, multiplexer_19_out, multiplexer_20_out, multiplexer_21_out,
       multiplexer_22_out, multiplexer_23_out, multiplexer_24_out, multiplexer_25_out, multiplexer_26_out,
       multiplexer_27_out, multiplexer_28_out, multiplexer_29_out, multiplexer_30_out, multiplexer_31_out,
       multiplexer_32_out, multiplexer_33_out, multiplexer_34_out, multiplexer_35_out, multiplexer_36_out,
       multiplexer_37_out, multiplexer_40_out, multiplexer_41_out, multiplexer_42_out, multiplexer_45_out,
       multiplexer_46_out, multiplexer_47_out, multiplexer_49_out, multiplexer_50_out, multiplexer_53_out,
       multiplexer_54_out, multiplexer_56_out, multiplexer_58_out, multiplexer_60_out, multiplexer_62_out,
       multiplexer_65_out, multiplexer_67_out, not_1_out, not_2_out, or_1_out, or_2_out, S, SA, SB, SC, SD,
       SE, SF, SG, SH, SI, SJ, STP, U_D;

  Multiplexer #(.enable("false")) multiplexer_1 (.in0(MI), .in1(I), .out(SI), .sel(not_1_out));
  Multiplexer #(.enable("false")) multiplexer_2 (.in0(MG), .in1(G), .out(SG), .sel(not_1_out));
  Multiplexer #(.enable("false")) multiplexer_3 (.in0(ME), .in1(E), .out(SE), .sel(not_1_out));
  Multiplexer #(.enable("false")) multiplexer_4 (.in0(MC), .in1(C), .out(SC), .sel(not_1_out));
  Multiplexer #(.enable("false")) multiplexer_5 (.in0(MA), .in1(A), .out(SA), .sel(not_1_out));
  not not_1 (not_1_out, STP);
  Multiplexer #(.enable("false")) multiplexer_6 (.in0(1'b0), .in1(1'b1), .out(multiplexer_6_out), .sel(CL1));
  Multiplexer #(.enable("false")) multiplexer_7 (.in0(CL0), .in1(1'b0), .out(multiplexer_7_out), .sel(CL1));
  Multiplexer #(.enable("false")) multiplexer_8 (.in0(MJ), .in1(J), .out(SJ), .sel(not_1_out));
  Multiplexer #(.enable("false")) multiplexer_9 (.in0(MH), .in1(H), .out(SH), .sel(not_1_out));
  Multiplexer #(.enable("false")) multiplexer_10 (.in0(MF), .in1(F), .out(SF), .sel(not_1_out));
  Multiplexer #(.enable("false")) multiplexer_11 (.in0(MD), .in1(D), .out(SD), .sel(not_1_out));
  Multiplexer #(.enable("false")) multiplexer_12 (.in0(MB), .in1(B), .out(SB), .sel(not_1_out));
  Multi multi_1 (
    .in_1(A), .in_2(B), .in_3(C), .in_4(D), .in_5(E), .in_6(F), .in_7(G), .in_8(H), .in_9(I), .in_10(J),
    .in_11(in_20), .in_12(in_19), .in_13(in_18), .in_14(in_17), .out_15(MA), .out_16(MB), .out_17(MC),
    .out_18(MD), .out_19(ME), .out_20(MF), .out_21(MG), .out_22(MH), .out_23(MI), .out_24(MJ));
  J_K_Flip_Flop #(.enable("true")) j_k_ff_1 (
    .J(in_2), .clk(S), .K(in_2), .Q(A), .Qn(j_k_ff_1_qn), .preset(multiplexer_6_out), .en(in_1),
    .reset(multiplexer_7_out));
  Multiplexer #(.enable("false")) multiplexer_13 (.in0(A), .in1(j_k_ff_1_qn), .out(multiplexer_13_out), .sel(U_D));
  Multiplexer #(.enable("false")) multiplexer_14 (.in0(1'b0), .in1(1'b1), .out(multiplexer_14_out), .sel(CL1));
  Multiplexer #(.enable("false")) multiplexer_15 (.in0(CL0), .in1(1'b0), .out(multiplexer_15_out), .sel(CL1));
  J_K_Flip_Flop #(.enable("true")) j_k_ff_2 (
    .J(in_2), .clk(multiplexer_13_out), .K(in_2), .Q(B), .Qn(j_k_ff_2_qn), .preset(multiplexer_14_out),
    .en(in_1), .reset(multiplexer_15_out));
  Multiplexer #(.enable("false")) multiplexer_16 (.in0(B), .in1(j_k_ff_2_qn), .out(multiplexer_16_out), .sel(U_D));
  BCD12BIT bcd12bit_1 (
    .in_1(in_8), .in_2(in_8), .in_3(SJ), .in_4(SI), .in_5(SH), .in_6(SG), .in_7(SF), .in_8(SE), .in_9(SD),
    .in_10(SC), .in_11(SB), .in_12(SA), .out_17(out_24), .out_18(out_25), .out_19(out_26), .out_20(out_27),
    .out_21(out_28), .out_22(out_29), .out_23(out_30), .out_24(out_31), .out_25(out_32), .out_26(out_33),
    .out_27(out_34), .out_28(out_35));  // open: out_13, out_14, out_15, out_16
  Multiplexer #(.enable("false")) multiplexer_17 (.in0(1'b0), .in1(1'b1), .out(multiplexer_17_out), .sel(CL1));
  Multiplexer #(.enable("false")) multiplexer_18 (.in0(CL0), .in1(1'b0), .out(multiplexer_18_out), .sel(CL1));
  J_K_Flip_Flop #(.enable("true")) j_k_ff_3 (
    .J(in_2), .clk(multiplexer_16_out), .K(in_2), .Q(C), .Qn(j_k_ff_3_qn), .preset(multiplexer_17_out),
    .en(in_1), .reset(multiplexer_18_out));
  Multiplexer #(.enable("false")) multiplexer_19 (.in0(C), .in1(j_k_ff_3_qn), .out(multiplexer_19_out), .sel(U_D));
  Multiplexer #(.enable("false")) multiplexer_20 (.in0(1'b0), .in1(1'b0), .out(multiplexer_20_out), .sel(CL1));
  Multiplexer #(.enable("false")) multiplexer_21 (.in0(CL0), .in1(1'b1), .out(multiplexer_21_out), .sel(CL1));
  Multiplexer #(.enable("false")) multiplexer_22 (.in0(B3), .in1(LB3), .out(multiplexer_22_out), .sel(BD_sb));
  COMP10bits comp10bits_1 (
    .in_21(1'b1), .in_22(in_22), .in_23(in_23), .out_24(comp10bits_1_out_24), .A_B(comp10bits_1_a_b),
    .A_B_2(comp10bits_1_a_b_2), .in_1(B9), .in_2(SJ), .in_3(B8), .in_4(SI), .in_5(B7), .in_6(SH), .in_7(B6),
    .in_8(SG), .in_9(B5), .in_10(SF), .in_11(B4), .in_12(SE), .in_13(multiplexer_22_out), .in_14(SD),
    .in_15(multiplexer_24_out), .in_16(SC), .in_17(multiplexer_23_out), .in_18(SB),
    .in_19(multiplexer_28_out), .in_20(SA));
  J_K_Flip_Flop #(.enable("true")) j_k_ff_4 (
    .J(in_2), .clk(multiplexer_19_out), .K(in_2), .Q(D), .Qn(j_k_ff_4_qn), .preset(multiplexer_20_out),
    .en(in_1), .reset(multiplexer_21_out));
  Multiplexer #(.enable("false")) multiplexer_23 (.in0(B1), .in1(LB1), .out(multiplexer_23_out), .sel(BD_sb));
  Multiplexer #(.enable("false")) multiplexer_24 (.in0(B2), .in1(LB2), .out(multiplexer_24_out), .sel(BD_sb));
  Multiplexer #(.enable("false")) multiplexer_25 (.in0(1'b0), .in1(1'b0), .out(multiplexer_25_out), .sel(CL1));
  Multiplexer #(.enable("false")) multiplexer_26 (.in0(D), .in1(j_k_ff_4_qn), .out(multiplexer_26_out), .sel(U_D));
  Multiplexer #(.enable("false")) multiplexer_27 (.in0(CL0), .in1(1'b1), .out(multiplexer_27_out), .sel(CL1));
  _7_Segment_Display u_7_segment_display_1 (.g(DG3), .f(DF3), .a(DA3), .b(DB3), .e(DE3), .d(DD3), .c(DC3), .dp(1'b0));
  _7447 #(.ShowInternalStructure("true")) u_7447_1 (
    .pin1(out_26), .pin2(out_25), .pin6(out_24), .pin7(out_27), .pin15(DF3), .pin14(DG3), .pin13(DA3),
    .pin12(DB3), .pin11(DC3), .pin10(DD3), .pin9(DE3));  // open: pin3, pin4, pin5
  Multiplexer #(.enable("false")) multiplexer_28 (.in0(B0), .in1(LB0), .out(multiplexer_28_out), .sel(BD_sb));
  or or_1 (or_1_out, comp10bits_1_a_b, comp10bits_1_out_24);
  or or_2 (or_2_out, comp10bits_1_out_24, comp10bits_1_a_b_2);
  J_K_Flip_Flop #(.enable("true")) j_k_ff_5 (
    .J(in_2), .clk(multiplexer_26_out), .K(in_2), .Q(E), .Qn(j_k_ff_5_qn), .preset(multiplexer_25_out),
    .en(in_1), .reset(multiplexer_27_out));
  Multiplexer #(.enable("false")) multiplexer_29 (.in0(1'b0), .in1(1'b1), .out(multiplexer_29_out), .sel(CL1));
  Multiplexer #(.enable("false")) multiplexer_30 (.in0(E), .in1(j_k_ff_5_qn), .out(multiplexer_30_out), .sel(U_D));
  Multiplexer #(.enable("false")) multiplexer_31 (.in0(CL0), .in1(1'b0), .out(multiplexer_31_out), .sel(CL1));
  _7_Segment_Display u_7_segment_display_2 (.g(DG2), .f(DF2), .a(DA2), .b(DB2), .e(DE2), .d(DD2), .c(DC2), .dp(1'b0));
  _7447 #(.ShowInternalStructure("true")) u_7447_2 (
    .pin1(out_30), .pin2(out_29), .pin6(out_28), .pin7(out_31), .pin15(DF2), .pin14(DG2), .pin13(DA2),
    .pin12(DB2), .pin11(DC2), .pin10(DD2), .pin9(DE2));  // open: pin3, pin4, pin5
  and and_1 (CL0, U_D, ~or_1_out);  // AND_Gate
  and and_2 (CL1, ~U_D, ~or_2_out);  // AND_Gate
  J_K_Flip_Flop #(.enable("true")) j_k_ff_6 (
    .J(in_2), .clk(multiplexer_30_out), .K(in_2), .Q(F), .Qn(j_k_ff_6_qn), .preset(multiplexer_29_out),
    .en(in_1), .reset(multiplexer_31_out));
  Multiplexer #(.enable("false")) multiplexer_32 (.in0(F), .in1(j_k_ff_6_qn), .out(multiplexer_32_out), .sel(U_D));
  _7_Segment_Display u_7_segment_display_3 (.g(DG1), .f(DF1), .a(DA1), .b(DB1), .e(DE1), .d(DD1), .c(DC1), .dp(1'b0));
  _7447 #(.ShowInternalStructure("true")) u_7447_3 (
    .pin1(out_34), .pin2(out_33), .pin6(out_32), .pin7(out_35), .pin15(DF1), .pin14(DG1), .pin13(DA1),
    .pin12(DB1), .pin11(DC1), .pin10(DD1), .pin9(DE1));  // open: pin3, pin4, pin5
  Multiplexer #(.enable("false")) multiplexer_33 (.in0(1'b0), .in1(1'b1), .out(multiplexer_33_out), .sel(CL1));
  J_K_Flip_Flop #(.enable("true")) j_k_ff_7 (
    .J(in_2), .clk(multiplexer_32_out), .K(in_2), .Q(G), .Qn(j_k_ff_7_qn), .preset(multiplexer_33_out),
    .en(in_1), .reset(multiplexer_34_out));
  Multiplexer #(.enable("false")) multiplexer_34 (.in0(CL0), .in1(1'b0), .out(multiplexer_34_out), .sel(CL1));
  Multiplexer #(.enable("false")) multiplexer_35 (.in0(G), .in1(j_k_ff_7_qn), .out(multiplexer_35_out), .sel(U_D));
  Multiplexer #(.enable("false")) multiplexer_36 (.in0(1'b0), .in1(1'b1), .out(multiplexer_36_out), .sel(CL1));
  J_K_Flip_Flop #(.enable("true")) j_k_ff_8 (
    .J(in_2), .clk(multiplexer_35_out), .K(in_2), .Q(H), .Qn(j_k_ff_8_qn), .preset(multiplexer_36_out),
    .en(in_1), .reset(multiplexer_37_out));
  Multiplexer #(.enable("false")) multiplexer_37 (.in0(CL0), .in1(1'b0), .out(multiplexer_37_out), .sel(CL1));
  Clock clock_1 (.out(S));
  Multiplexer #(.enable("false")) multiplexer_38 (.in0(in_3), .in1(1'b1), .out(U_D), .sel(in_6));
  Multiplexer #(.enable("false")) multiplexer_39 (.in0(in_4), .in1(1'b0), .out(STP), .sel(in_6));
  Multiplexer #(.enable("false")) multiplexer_40 (.in0(H), .in1(j_k_ff_8_qn), .out(multiplexer_40_out), .sel(U_D));
  Multiplexer #(.enable("false")) multiplexer_41 (.in0(1'b0), .in1(1'b1), .out(multiplexer_41_out), .sel(CL1));
  J_K_Flip_Flop #(.enable("true")) j_k_ff_9 (
    .J(in_2), .clk(multiplexer_40_out), .K(in_2), .Q(I), .Qn(j_k_ff_9_qn), .preset(multiplexer_41_out),
    .en(in_1), .reset(multiplexer_42_out));
  Multiplexer #(.enable("false")) multiplexer_42 (.in0(CL0), .in1(1'b0), .out(multiplexer_42_out), .sel(CL1));
  Multiplexer #(.enable("false")) multiplexer_43 (.in0(LOAD), .in1(1'b0), .out(LD), .sel(in_6));
  Multiplexer #(.enable("false")) multiplexer_44 (.in0(in_7), .in1(1'b0), .out(MA_MI), .sel(in_6));
  LOAD4bits load4bits_1 (
    .in_4(in_20), .in_5(in_19), .in_6(in_18), .in_7(in_17), .LOAD(LD), .CLK(S), .RESET(in_21), .out_8(LB0),
    .out_9(LB1), .out_10(LB2), .out_11(LB3));
  J_K_Flip_Flop #(.enable("true")) j_k_ff_10 (
    .J(1'b1), .clk(LD), .K(1'b1), .Q(j_k_ff_10_q), .en(1'b1));  // open: Qn, preset, reset
  Multiplexer #(.enable("false")) multiplexer_45 (.in0(I), .in1(j_k_ff_9_qn), .out(multiplexer_45_out), .sel(U_D));
  and and_3 (BD_sb, ~LD, j_k_ff_10_q);  // AND_Gate
  Multiplexer #(.enable("false")) multiplexer_46 (.in0(1'b0), .in1(1'b1), .out(multiplexer_46_out), .sel(CL1));
  J_K_Flip_Flop #(.enable("true")) j_k_ff_11 (
    .J(in_2), .clk(multiplexer_45_out), .K(in_2), .Q(J), .preset(multiplexer_46_out), .en(in_1),
    .reset(multiplexer_47_out));  // open: Qn
  Multiplexer #(.enable("false")) multiplexer_47 (.in0(CL0), .in1(1'b0), .out(multiplexer_47_out), .sel(CL1));
  not not_2 (not_2_out, MA_MI);
  Multiplexer #(.enable("false")) multiplexer_48 (.in0(in_11), .in1(multiplexer_54_out), .out(B9), .sel(not_2_out));
  Multiplexer #(.enable("false")) multiplexer_49 (.in0(1'b0), .in1(1'b0), .out(multiplexer_49_out), .sel(U_D));
  Multiplexer #(.enable("false")) multiplexer_50 (.in0(1'b0), .in1(1'b0), .out(multiplexer_50_out), .sel(U_D));
  Multiplexer #(.enable("false")) multiplexer_51 (.in0(in_17), .in1(multiplexer_50_out), .out(B3), .sel(not_2_out));
  Multiplexer #(.enable("false")) multiplexer_52 (.in0(in_16), .in1(multiplexer_49_out), .out(B4), .sel(not_2_out));
  Multiplexer #(.enable("false")) multiplexer_53 (.in0(1'b0), .in1(1'b1), .out(multiplexer_53_out), .sel(U_D));
  Multiplexer #(.enable("false")) multiplexer_54 (.in0(1'b0), .in1(1'b1), .out(multiplexer_54_out), .sel(U_D));
  Multiplexer #(.enable("false")) multiplexer_55 (.in0(in_12), .in1(multiplexer_53_out), .out(B8), .sel(not_2_out));
  Multiplexer #(.enable("false")) multiplexer_56 (.in0(1'b0), .in1(1'b1), .out(multiplexer_56_out), .sel(U_D));
  Multiplexer #(.enable("false")) multiplexer_57 (.in0(in_18), .in1(multiplexer_56_out), .out(B2), .sel(not_2_out));
  Multiplexer #(.enable("false")) multiplexer_58 (.in0(1'b0), .in1(1'b1), .out(multiplexer_58_out), .sel(U_D));
  Multiplexer #(.enable("false")) multiplexer_59 (.in0(in_13), .in1(multiplexer_58_out), .out(B7), .sel(not_2_out));
  Multiplexer #(.enable("false")) multiplexer_60 (.in0(1'b0), .in1(1'b1), .out(multiplexer_60_out), .sel(U_D));
  Multiplexer #(.enable("false")) multiplexer_61 (.in0(in_19), .in1(multiplexer_60_out), .out(B1), .sel(not_2_out));
  Multiplexer #(.enable("false")) multiplexer_62 (.in0(1'b0), .in1(1'b1), .out(multiplexer_62_out), .sel(U_D));
  Multiplexer #(.enable("false")) multiplexer_63 (.in0(in_14), .in1(multiplexer_62_out), .out(B6), .sel(not_2_out));
  Multiplexer #(.enable("false")) multiplexer_64 (.in0(in_15), .in1(multiplexer_67_out), .out(B5), .sel(not_2_out));
  Multiplexer #(.enable("false")) multiplexer_65 (.in0(1'b0), .in1(1'b1), .out(multiplexer_65_out), .sel(U_D));
  Multiplexer #(.enable("false")) multiplexer_66 (.in0(in_20), .in1(multiplexer_65_out), .out(B0), .sel(not_2_out));
  Multiplexer #(.enable("false")) multiplexer_67 (.in0(1'b0), .in1(1'b1), .out(multiplexer_67_out), .sel(U_D));

  // Other names for the same wires on the sheet: B10 = in_10; B11 = in_9; bb0 = in_20; bb1 = in_19; bb2 = in_18;
  //   bb3 = in_17; bb4 = in_16; bb5 = in_15; bb6 = in_14; bb7 = in_13; bb8 = in_12; bb9 = in_11; CEN0 = out_27;
  //   CEN1 = out_26; CEN2 = out_25; CEN3 = out_24; CLR = in_6; DEN0 = out_31; DEN1 = out_30; DEN2 = out_29;
  //   DEN3 = out_28; Ena = in_2; LD0 = LOAD; MA_MI0 = in_7; STP0 = in_4; U_D0 = in_3; UN0 = out_35; UN1 = out_34;
  //   UN2 = out_33; UN3 = out_32

  // Notes on the sheet:
  //   LIMIT SUP(ACR - 0)
  //   LIMIT DEC(DEC - 999)
  //   UP / DOWN
  //   STEP
  //   CLEAR
  //   LIMITE
endmodule

module COMP (
  input  in_1,
  input  in_2,
  input  in_3,
  input  in_4,
  input  in_5,
  input  in_6,
  input  in_7,
  input  in_8,
  input  in_9,
  input  in_10,
  input  in_11,
  input  in_12,
  input  in_13,
  input  in_14,
  input  in_15,
  input  in_16,
  input  in_17,
  input  in_18,
  input  in_19,
  input  in_20,
  output out_21
);

  wire xnor_1_out, xnor_2_out, xnor_3_out, xnor_4_out, xnor_5_out, xnor_6_out, xnor_7_out, xnor_8_out,
       xnor_9_out, xnor_10_out;

  xnor xnor_1 (xnor_1_out, in_1, in_2);
  xnor xnor_2 (xnor_2_out, in_3, in_4);
  xnor xnor_3 (xnor_3_out, in_5, in_6);
  xnor xnor_4 (xnor_4_out, in_7, in_8);
  xnor xnor_5 (xnor_5_out, in_9, in_10);
  xnor xnor_6 (xnor_6_out, in_11, in_12);
  xnor xnor_7 (xnor_7_out, in_13, in_14);
  xnor xnor_8 (xnor_8_out, in_15, in_16);
  xnor xnor_9 (xnor_9_out, in_17, in_18);
  xnor xnor_10 (xnor_10_out, in_19, in_20);
  and and_1 (out_21, xnor_1_out, xnor_2_out, xnor_3_out, xnor_4_out, xnor_5_out, xnor_6_out, xnor_7_out, xnor_8_out, xnor_9_out, xnor_10_out);
endmodule

module LOAD10bits (
  input  in_1,
  input  in_2,
  input  in_3,
  input  in_4,
  input  in_5,
  input  in_6,
  input  in_7,
  input  in_8,
  input  in_9,
  input  in_10,
  input  in_11,
  input  in_12,
  input  in_13,
  output out_14,
  output out_15,
  output out_16,
  output out_17,
  output out_18,
  output out_19,
  output out_20,
  output out_21,
  output out_22,
  output out_23
);

  wire and_1_out, and_2_out, and_3_out, and_4_out, and_5_out, and_6_out, and_7_out, and_8_out, and_9_out,
       and_10_out, and_11_out, and_12_out, and_13_out, and_14_out, and_15_out, and_16_out, and_17_out,
       and_18_out, and_19_out, and_20_out, or_1_out, or_2_out, or_3_out, or_4_out, or_5_out, or_6_out,
       or_7_out, or_8_out, or_9_out, or_10_out;

  and and_1 (and_1_out, out_14, ~in_2);  // AND_Gate
  and and_2 (and_2_out, in_2, in_4);
  and and_3 (and_3_out, out_15, ~in_2);  // AND_Gate
  and and_4 (and_4_out, in_2, in_5);
  and and_5 (and_5_out, out_16, ~in_2);  // AND_Gate
  and and_6 (and_6_out, in_2, in_6);
  and and_7 (and_7_out, out_17, ~in_2);  // AND_Gate
  and and_8 (and_8_out, in_2, in_7);
  and and_9 (and_9_out, out_18, ~in_2);  // AND_Gate
  and and_10 (and_10_out, in_2, in_8);
  and and_11 (and_11_out, out_19, ~in_2);  // AND_Gate
  and and_12 (and_12_out, in_2, in_9);
  and and_13 (and_13_out, out_20, ~in_2);  // AND_Gate
  and and_14 (and_14_out, in_2, in_10);
  and and_15 (and_15_out, out_21, ~in_2);  // AND_Gate
  and and_16 (and_16_out, in_2, in_11);
  and and_17 (and_17_out, out_22, ~in_2);  // AND_Gate
  and and_18 (and_18_out, in_2, in_12);
  and and_19 (and_19_out, out_23, ~in_2);  // AND_Gate
  and and_20 (and_20_out, in_2, in_13);
  or or_1 (or_1_out, and_1_out, and_2_out);
  or or_2 (or_2_out, and_3_out, and_4_out);
  or or_3 (or_3_out, and_5_out, and_6_out);
  or or_4 (or_4_out, and_7_out, and_8_out);
  or or_5 (or_5_out, and_9_out, and_10_out);
  or or_6 (or_6_out, and_11_out, and_12_out);
  or or_7 (or_7_out, and_13_out, and_14_out);
  or or_8 (or_8_out, and_15_out, and_16_out);
  or or_9 (or_9_out, and_17_out, and_18_out);
  or or_10 (or_10_out, and_19_out, and_20_out);
  D_Flip_Flop #(.Pre_Clr_Positions("LEGACY"), .enable("true")) d_ff_1 (
    .clk(in_1), .D(or_1_out), .Q(out_14), .reset(in_3));  // open: Qn, preset, en
  D_Flip_Flop #(.Pre_Clr_Positions("LEGACY"), .enable("true")) d_ff_2 (
    .clk(in_1), .D(or_2_out), .Q(out_15), .reset(in_3));  // open: Qn, preset, en
  D_Flip_Flop #(.Pre_Clr_Positions("LEGACY"), .enable("true")) d_ff_3 (
    .clk(in_1), .D(or_3_out), .Q(out_16), .reset(in_3));  // open: Qn, preset, en
  D_Flip_Flop #(.Pre_Clr_Positions("LEGACY"), .enable("true")) d_ff_4 (
    .clk(in_1), .D(or_4_out), .Q(out_17), .reset(in_3));  // open: Qn, preset, en
  D_Flip_Flop #(.Pre_Clr_Positions("LEGACY"), .enable("true")) d_ff_5 (
    .clk(in_1), .D(or_5_out), .Q(out_18), .reset(in_3));  // open: Qn, preset, en
  D_Flip_Flop #(.Pre_Clr_Positions("LEGACY"), .enable("true")) d_ff_6 (
    .clk(in_1), .D(or_6_out), .Q(out_19), .reset(in_3));  // open: Qn, preset, en
  D_Flip_Flop #(.Pre_Clr_Positions("LEGACY"), .enable("true")) d_ff_7 (
    .clk(in_1), .D(or_7_out), .Q(out_20), .reset(in_3));  // open: Qn, preset, en
  D_Flip_Flop #(.Pre_Clr_Positions("LEGACY"), .enable("true")) d_ff_8 (
    .clk(in_1), .D(or_8_out), .Q(out_21), .reset(in_3));  // open: Qn, preset, en
  D_Flip_Flop #(.Pre_Clr_Positions("LEGACY"), .enable("true")) d_ff_9 (
    .clk(in_1), .D(or_9_out), .Q(out_22), .reset(in_3));  // open: Qn, preset, en
  D_Flip_Flop #(.Pre_Clr_Positions("LEGACY"), .enable("true")) d_ff_10 (
    .clk(in_1), .D(or_10_out), .Q(out_23), .reset(in_3));  // open: Qn, preset, en
endmodule

module Multi (
  input  in_1,
  input  in_2,
  input  in_3,
  input  in_4,
  input  in_5,
  input  in_6,
  input  in_7,
  input  in_8,
  input  in_9,
  input  in_10,
  input  in_11,
  input  in_12,
  input  in_13,
  input  in_14,
  output out_15,
  output out_16,
  output out_17,
  output out_18,
  output out_19,
  output out_20,
  output out_21,
  output out_22,
  output out_23,
  output out_24
);

  wire [9:0] multiplier_1_cout;

  Multiplier #(.width(10)) multiplier_1 (
    .a({in_10, in_9, in_8, in_7, in_6, in_5, in_4, in_3, in_2, in_1}),
    .b({{6{1'b0}}, in_14, in_13, in_12, in_11}),
    .out({out_24, out_23, out_22, out_21, out_20, out_19, out_18, out_17, out_16, out_15}), .cin({10{1'b0}}),
    .cout(multiplier_1_cout));
endmodule

module COMP1bits (
  input  A_B,
  input  A,
  input  B,
  input  A_B_2,
  input  A_B_3,
  output S_A_B,
  output S_A_B_2,
  output S_A_B_3
);

  wire and_2_out, and_3_out, and_4_out, and_5_out, xnor_1_out;

  and and_1 (S_A_B, A_B, xnor_1_out);
  xnor xnor_1 (xnor_1_out, A, B);
  and and_2 (and_2_out, A_B, and_3_out);
  and and_3 (and_3_out, ~B, A);  // AND_Gate
  and and_4 (and_4_out, A_B, and_5_out);
  and and_5 (and_5_out, B, ~A);  // AND_Gate
  or or_1 (S_A_B_2, and_2_out, A_B_2);
  or or_2 (S_A_B_3, and_4_out, A_B_3);
endmodule

module COMP10bits (
  input  in_1,
  input  in_2,
  input  in_3,
  input  in_4,
  input  in_5,
  input  in_6,
  input  in_7,
  input  in_8,
  input  in_9,
  input  in_10,
  input  in_11,
  input  in_12,
  input  in_13,
  input  in_14,
  input  in_15,
  input  in_16,
  input  in_17,
  input  in_18,
  input  in_19,
  input  in_20,
  input  in_21,
  input  in_22,
  input  in_23,
  output out_24,
  output A_B,
  output A_B_2
);

  wire comp1bits_1_s_a_b, comp1bits_1_s_a_b_2, comp1bits_1_s_a_b_3, comp1bits_2_s_a_b, comp1bits_2_s_a_b_2,
       comp1bits_2_s_a_b_3, comp1bits_3_s_a_b, comp1bits_3_s_a_b_2, comp1bits_3_s_a_b_3, comp1bits_4_s_a_b,
       comp1bits_4_s_a_b_2, comp1bits_4_s_a_b_3, comp1bits_5_s_a_b, comp1bits_5_s_a_b_2, comp1bits_5_s_a_b_3,
       comp1bits_6_s_a_b, comp1bits_6_s_a_b_2, comp1bits_6_s_a_b_3, comp1bits_7_s_a_b, comp1bits_7_s_a_b_2,
       comp1bits_7_s_a_b_3, comp1bits_8_s_a_b, comp1bits_8_s_a_b_2, comp1bits_8_s_a_b_3, comp1bits_9_s_a_b,
       comp1bits_9_s_a_b_2, comp1bits_9_s_a_b_3;

  COMP1bits comp1bits_1 (
    .A_B(in_21), .A(in_1), .B(in_2), .A_B_2(in_22), .A_B_3(in_23), .S_A_B(comp1bits_1_s_a_b),
    .S_A_B_2(comp1bits_1_s_a_b_2), .S_A_B_3(comp1bits_1_s_a_b_3));
  COMP1bits comp1bits_2 (
    .A_B(comp1bits_1_s_a_b), .A(in_3), .B(in_4), .A_B_2(comp1bits_1_s_a_b_2), .A_B_3(comp1bits_1_s_a_b_3),
    .S_A_B(comp1bits_2_s_a_b), .S_A_B_2(comp1bits_2_s_a_b_2), .S_A_B_3(comp1bits_2_s_a_b_3));
  COMP1bits comp1bits_3 (
    .A_B(comp1bits_2_s_a_b), .A(in_5), .B(in_6), .A_B_2(comp1bits_2_s_a_b_2), .A_B_3(comp1bits_2_s_a_b_3),
    .S_A_B(comp1bits_3_s_a_b), .S_A_B_2(comp1bits_3_s_a_b_2), .S_A_B_3(comp1bits_3_s_a_b_3));
  COMP1bits comp1bits_4 (
    .A_B(comp1bits_3_s_a_b), .A(in_7), .B(in_8), .A_B_2(comp1bits_3_s_a_b_2), .A_B_3(comp1bits_3_s_a_b_3),
    .S_A_B(comp1bits_4_s_a_b), .S_A_B_2(comp1bits_4_s_a_b_2), .S_A_B_3(comp1bits_4_s_a_b_3));
  COMP1bits comp1bits_5 (
    .A_B(comp1bits_4_s_a_b), .A(in_9), .B(in_10), .A_B_2(comp1bits_4_s_a_b_2), .A_B_3(comp1bits_4_s_a_b_3),
    .S_A_B(comp1bits_5_s_a_b), .S_A_B_2(comp1bits_5_s_a_b_2), .S_A_B_3(comp1bits_5_s_a_b_3));
  COMP1bits comp1bits_6 (
    .A_B(comp1bits_5_s_a_b), .A(in_11), .B(in_12), .A_B_2(comp1bits_5_s_a_b_2), .A_B_3(comp1bits_5_s_a_b_3),
    .S_A_B(comp1bits_6_s_a_b), .S_A_B_2(comp1bits_6_s_a_b_2), .S_A_B_3(comp1bits_6_s_a_b_3));
  COMP1bits comp1bits_7 (
    .A_B(comp1bits_6_s_a_b), .A(in_13), .B(in_14), .A_B_2(comp1bits_6_s_a_b_2), .A_B_3(comp1bits_6_s_a_b_3),
    .S_A_B(comp1bits_7_s_a_b), .S_A_B_2(comp1bits_7_s_a_b_2), .S_A_B_3(comp1bits_7_s_a_b_3));
  COMP1bits comp1bits_8 (
    .A_B(comp1bits_7_s_a_b), .A(in_15), .B(in_16), .A_B_2(comp1bits_7_s_a_b_2), .A_B_3(comp1bits_7_s_a_b_3),
    .S_A_B(comp1bits_8_s_a_b), .S_A_B_2(comp1bits_8_s_a_b_2), .S_A_B_3(comp1bits_8_s_a_b_3));
  COMP1bits comp1bits_9 (
    .A_B(comp1bits_8_s_a_b), .A(in_17), .B(in_18), .A_B_2(comp1bits_8_s_a_b_2), .A_B_3(comp1bits_8_s_a_b_3),
    .S_A_B(comp1bits_9_s_a_b), .S_A_B_2(comp1bits_9_s_a_b_2), .S_A_B_3(comp1bits_9_s_a_b_3));
  COMP1bits comp1bits_10 (
    .A_B(comp1bits_9_s_a_b), .A(in_19), .B(in_20), .A_B_2(comp1bits_9_s_a_b_2), .A_B_3(comp1bits_9_s_a_b_3),
    .S_A_B(out_24), .S_A_B_2(A_B), .S_A_B_3(A_B_2));
endmodule

module LOAD4bits (
  input  LOAD,
  input  CLK,
  input  RESET,
  input  in_4,
  input  in_5,
  input  in_6,
  input  in_7,
  output out_8,
  output out_9,
  output out_10,
  output out_11
);

  wire and_1_out, and_2_out, and_3_out, and_4_out, and_5_out, and_6_out, and_7_out, and_8_out, or_1_out,
       or_2_out, or_3_out, or_4_out;

  and and_1 (and_1_out, out_8, ~LOAD);  // AND_Gate
  and and_2 (and_2_out, LOAD, in_4);
  and and_3 (and_3_out, out_9, ~LOAD);  // AND_Gate
  and and_4 (and_4_out, LOAD, in_5);
  and and_5 (and_5_out, out_10, ~LOAD);  // AND_Gate
  and and_6 (and_6_out, LOAD, in_6);
  and and_7 (and_7_out, out_11, ~LOAD);  // AND_Gate
  and and_8 (and_8_out, LOAD, in_7);
  or or_1 (or_1_out, and_1_out, and_2_out);
  or or_2 (or_2_out, and_3_out, and_4_out);
  or or_3 (or_3_out, and_5_out, and_6_out);
  or or_4 (or_4_out, and_7_out, and_8_out);
  D_Flip_Flop #(.Pre_Clr_Positions("LEGACY"), .enable("true")) d_ff_1 (
    .clk(CLK), .D(or_1_out), .Q(out_8), .reset(RESET));  // open: Qn, preset, en
  D_Flip_Flop #(.Pre_Clr_Positions("LEGACY"), .enable("true")) d_ff_2 (
    .clk(CLK), .D(or_2_out), .Q(out_9), .reset(RESET));  // open: Qn, preset, en
  D_Flip_Flop #(.Pre_Clr_Positions("LEGACY"), .enable("true")) d_ff_3 (
    .clk(CLK), .D(or_3_out), .Q(out_10), .reset(RESET));  // open: Qn, preset, en
  D_Flip_Flop #(.Pre_Clr_Positions("LEGACY"), .enable("true")) d_ff_4 (
    .clk(CLK), .D(or_4_out), .Q(out_11), .reset(RESET));  // open: Qn, preset, en
endmodule
