// Logisim project TEO06.circ as structural Verilog: 7 circuits, main circuit main
module main (
  input  in_1,
  input  in_2,
  input  in_3,
  input  in_4,
  input  in_5,
  input  in_6,
  input  in_7,
  input  in_8,
  input  in_9,
  input  in_10,
  input  in_11,
  input  in_12,
  input  in_13,
  input  in_14,
  input  in_15,
  input  in_16,
  input  in_17,
  input  in_18,
  input  in_19,
  input  in_20,
  input  in_21,
  input  in_22,
  input  in_23,
  input  in_24,
  input  in_25,
  output out_26,
  output out_27
);

  wire _5s, ADD, and_1_out, and_2_out, B, CANCD, CANCQ, CLK, COMP, D0, D1, D2, d_ff_1_q, d_ff_2_q, d_ff_3_q,
       d_ff_4_q, d_ff_5_q, d_ff_6_q, d_ff_10_q, d_ff_11_q, d_ff_12_q, d_ff_13_q, d_ff_14_q, d_ff_15_q,
       d_ff_16_q, d_ff_17_q, d_ff_18_q, d_ff_20_q, d_ff_21_q, d_ff_22_q, mde3_1_b, mde3_1_g, mde3_1_r,
       multiplexer_1_out, PWR_out, Q0, Q1, Q2, store_1_out_11, store_1_out_12, store_1_out_13,
       store_1_out_14, store_1_out_15, store_1_out_16, store_1_out_17, store_1_out_18, store_1_out_19,
       store_1_out_20, store_1_out_21, store_1_out_22, store_1_out_23, store_1_out_24, store_1_out_25,
       store_1_out_26, store_1_out_27, store_1_out_28, TD5, TD20, TQ20, tunnel;

  Multiplexer #(.enable("false")) multiplexer_1 (.in0(TD20), .in1(1'b1), .out(multiplexer_1_out), .sel(d_ff_10_q));
  Clock clock_1 (.out(CLK));
  D_Flip_Flop d_ff_1 (.clk(CLK), .D(TD5), .Q(d_ff_1_q));  // open: Qn, preset, reset
  D_Flip_Flop d_ff_2 (.clk(CLK), .D(CANCD), .Q(d_ff_2_q));  // open: Qn, preset, reset
  D_Flip_Flop d_ff_3 (.clk(CLK), .D(multiplexer_1_out), .Q(d_ff_3_q), .reset(d_ff_21_q));  // open: Qn, preset
  Button PWR (.out(PWR_out));
  Button u_ADD (.out(ADD));
  D_Flip_Flop d_ff_4 (.clk(CLK), .D(d_ff_1_q), .Q(d_ff_4_q));  // open: Qn, preset, reset
  D_Flip_Flop d_ff_5 (.clk(CLK), .D(d_ff_2_q), .Q(d_ff_5_q));  // open: Qn, preset, reset
  D_Flip_Flop d_ff_6 (.clk(CLK), .D(d_ff_3_q), .Q(d_ff_6_q), .reset(d_ff_21_q));  // open: Qn, preset
  MDE3 mde3_1 (
    .Q2(Q2), .Q1(Q1), .Q0(Q0), .Comp(COMP), .T20(TQ20), .T5(B), .CANC(CANCQ), .PWR(PWR_out), .ADD(ADD),
    .R(mde3_1_r), .G(mde3_1_g), .B(mde3_1_b), .DIS(out_26), .D2(D2), .D1(D1), .D0(D0), .TD5(TD5),
    .TD20(TD20), .CANC2(CANCD), .OUT(out_27));
  D_Flip_Flop d_ff_7 (.clk(CLK), .D(D2), .Q(Q2));  // open: Qn, preset, reset
  D_Flip_Flop d_ff_8 (.clk(CLK), .D(D1), .Q(Q1));  // open: Qn, preset, reset
  D_Flip_Flop d_ff_9 (.clk(CLK), .D(D0), .Q(Q0));  // open: Qn, preset, reset
  D_Flip_Flop d_ff_10 (.clk(d_ff_21_q), .D(1'b1), .Q(d_ff_10_q), .reset(d_ff_22_q));  // open: Qn, preset
  D_Flip_Flop d_ff_11 (.clk(CLK), .D(d_ff_4_q), .Q(d_ff_11_q));  // open: Qn, preset, reset
  D_Flip_Flop d_ff_12 (.clk(CLK), .D(d_ff_5_q), .Q(d_ff_12_q));  // open: Qn, preset, reset
  D_Flip_Flop d_ff_13 (.clk(CLK), .D(d_ff_6_q), .Q(d_ff_13_q), .reset(d_ff_21_q));  // open: Qn, preset
  D_Flip_Flop d_ff_14 (.clk(d_ff_21_q), .D(d_ff_10_q), .Q(d_ff_14_q), .reset(d_ff_22_q));  // open: Qn, preset
  // RGBLed rgbled_1: pin names not known; wires that end beside it: mde3_1_r, mde3_1_g, mde3_1_b
  D_Flip_Flop d_ff_15 (.clk(CLK), .D(d_ff_11_q), .Q(d_ff_15_q));  // open: Qn, preset, reset
  D_Flip_Flop d_ff_16 (.clk(CLK), .D(d_ff_12_q), .Q(d_ff_16_q));  // open: Qn, preset, reset
  D_Flip_Flop d_ff_17 (.clk(CLK), .D(d_ff_13_q), .Q(d_ff_17_q), .reset(d_ff_21_q));  // open: Qn, preset
  D_Flip_Flop d_ff_18 (.clk(d_ff_21_q), .D(d_ff_14_q), .Q(d_ff_18_q), .reset(d_ff_22_q));  // open: Qn, preset
  D_Flip_Flop d_ff_19 (.clk(CLK), .D(d_ff_15_q), .Q(_5s));  // open: Qn, preset, reset
  D_Flip_Flop d_ff_20 (.clk(CLK), .D(d_ff_16_q), .Q(d_ff_20_q));  // open: Qn, preset, reset
  D_Flip_Flop d_ff_21 (.clk(CLK), .D(d_ff_17_q), .Q(d_ff_21_q), .reset(d_ff_21_q));  // open: Qn, preset
  D_Flip_Flop d_ff_22 (.clk(d_ff_21_q), .D(d_ff_18_q), .Q(d_ff_22_q), .reset(d_ff_22_q));  // open: Qn, preset
  or or_1 (B, d_ff_1_q, d_ff_4_q, d_ff_11_q, d_ff_15_q, _5s);
  or or_2 (CANCQ, d_ff_2_q, d_ff_5_q, d_ff_12_q, d_ff_16_q, d_ff_20_q);
  or or_3 (TQ20, d_ff_3_q, d_ff_6_q, d_ff_13_q, d_ff_17_q, d_ff_21_q, d_ff_10_q);
  STORE store_1 (
    .in_7(Q0), .in_8(Q1), .in_9(CLK), .in_1(in_5), .in_2(in_6), .in_3(in_7), .in_4(in_8), .in_5(in_9),
    .in_6(in_10), .in_10(and_1_out), .out_11(store_1_out_11), .out_12(store_1_out_12),
    .out_13(store_1_out_13), .out_14(store_1_out_14), .out_15(store_1_out_15), .out_16(store_1_out_16),
    .out_17(store_1_out_17), .out_18(store_1_out_18), .out_19(store_1_out_19), .out_20(store_1_out_20),
    .out_21(store_1_out_21), .out_22(store_1_out_22), .out_23(store_1_out_23), .out_24(store_1_out_24),
    .out_25(store_1_out_25), .out_26(store_1_out_26), .out_27(store_1_out_27), .out_28(store_1_out_28));
  and and_1 (and_1_out, ~Q2, ~Q1, ~Q0);  // AND_Gate
  COMP_18 comp_18_1 (
    .in_1(store_1_out_11), .in_3(store_1_out_12), .in_5(store_1_out_13), .in_7(store_1_out_14),
    .in_9(store_1_out_15), .in_11(store_1_out_16), .in_13(store_1_out_17), .in_15(store_1_out_18),
    .in_17(store_1_out_19), .in_19(store_1_out_20), .in_21(store_1_out_21), .in_23(store_1_out_22),
    .in_25(store_1_out_23), .in_27(store_1_out_24), .in_29(store_1_out_25), .in_31(store_1_out_26),
    .in_33(store_1_out_27), .in_35(store_1_out_28), .out_37(tunnel), .in_2(in_1), .in_4(in_2), .in_6(in_3),
    .in_8(in_4), .in_10(in_11), .in_12(in_12), .in_14(in_13), .in_16(in_14), .in_18(in_15), .in_20(in_16),
    .in_22(in_17), .in_24(in_18), .in_26(in_19), .in_28(in_20), .in_30(in_21), .in_32(in_22), .in_34(in_23),
    .in_36(in_24));
  and and_2 (and_2_out, Q2, ~Q1, ~Q0, _5s);  // AND_Gate
  Multiplexer #(.enable("false")) multiplexer_2 (.in0(in_25), .in1(tunnel), .out(COMP), .sel(and_2_out));

  // Other names for the same wires on the sheet: B0 = in_10; B1 = in_9; B2 = in_8; B3 = in_7; B4 = in_6; B5 = in_5;
  //   TQ5 = B
endmodule

module Maquina_de_Estados (
  input  Q2,
  input  Q1,
  input  Q0,
  input  PWR,
  input  ADD,
  output R,
  output G,
  output B,
  output OUT,
  output DISPLAY,
  output D2,
  output D1,
  output D0
);

  wire and_1_out, and_2_out, and_3_out, and_4_out, and_5_out, and_6_out, and_7_out, and_8_out, and_9_out,
       and_10_out, and_11_out, and_13_out, and_14_out, and_15_out, and_16_out, and_17_out, and_18_out,
       not_1_out, not_2_out, not_3_out, not_4_out, not_5_out, not_6_out, not_7_out, not_8_out, not_9_out,
       not_10_out, not_11_out, not_12_out, not_13_out, not_14_out, not_15_out, not_16_out, not_17_out,
       not_18_out, not_19_out, not_20_out, not_21_out, not_22_out, not_23_out, not_24_out, not_25_out,
       not_26_out, not_27_out, not_28_out, not_29_out, not_30_out, not_31_out, not_32_out, not_33_out,
       not_34_out, not_35_out, not_36_out, not_37_out, not_38_out, not_39_out, not_40_out, not_41_out,
       not_42_out, not_43_out, not_44_out, not_45_out, not_46_out, not_47_out, not_48_out;

  not not_1 (not_1_out, Q2);
  not not_2 (not_2_out, Q1);
  not not_3 (not_3_out, Q0);
  not not_4 (not_4_out, PWR);
  not not_5 (not_5_out, Q1);
  not not_6 (not_6_out, Q0);
  not not_7 (not_7_out, PWR);
  not not_8 (not_8_out, ADD);
  not not_9 (not_9_out, Q2);
  not not_10 (not_10_out, Q2);
  not not_11 (not_11_out, ADD);
  not not_12 (not_12_out, Q2);
  not not_13 (not_13_out, ADD);
  not not_14 (not_14_out, Q2);
  not not_15 (not_15_out, Q1);
  not not_16 (not_16_out, Q0);
  not not_17 (not_17_out, ADD);
  not not_18 (not_18_out, Q2);
  not not_19 (not_19_out, PWR);
  not not_20 (not_20_out, Q2);
  not not_21 (not_21_out, PWR);
  not not_22 (not_22_out, Q2);
  not not_23 (not_23_out, Q2);
  not not_24 (not_24_out, Q1);
  not not_25 (not_25_out, Q0);
  not not_26 (not_26_out, PWR);
  not not_27 (not_27_out, ADD);
  not not_28 (not_28_out, Q2);
  not not_29 (not_29_out, PWR);
  not not_30 (not_30_out, Q2);
  not not_31 (not_31_out, Q1);
  not not_32 (not_32_out, PWR);
  not not_33 (not_33_out, Q2);
  not not_34 (not_34_out, Q0);
  not not_35 (not_35_out, PWR);
  not not_36 (not_36_out, Q2);
  not not_37 (not_37_out, PWR);
  not not_38 (not_38_out, ADD);
  not not_39 (not_39_out, Q2);
  not not_40 (not_40_out, Q1);
  not not_41 (not_41_out, Q0);
  not not_42 (not_42_out, ADD);
  not not_43 (not_43_out, Q2);
  not not_44 (not_44_out, PWR);
  not not_45 (not_45_out, ADD);
  not not_46 (not_46_out, Q2);
  not not_47 (not_47_out, Q0);
  not not_48 (not_48_out, PWR);
  and and_1 (and_1_out, not_1_out, not_2_out, not_3_out, not_4_out);
  and and_2 (and_2_out, not_5_out, not_6_out, not_7_out, not_8_out);
  and and_3 (and_3_out, not_9_out, PWR, ADD);
  and and_4 (and_4_out, not_10_out, Q0, not_11_out);
  and and_5 (and_5_out, not_12_out, Q1, not_13_out);
  and and_6 (and_6_out, not_14_out, not_15_out, not_16_out, PWR, not_17_out);
  and and_7 (and_7_out, not_18_out, Q0, not_19_out, ADD);
  and and_8 (and_8_out, not_20_out, Q1, not_21_out, ADD);
  and and_9 (and_9_out, not_22_out, Q0);
  and and_10 (and_10_out, not_23_out, Q1);
  and and_11 (and_11_out, Q2, not_24_out, not_25_out, not_26_out, not_27_out);
  and and_12 (D2, not_28_out, Q1, Q0, not_29_out, ADD);
  and and_13 (and_13_out, not_30_out, not_31_out, Q0, not_32_out, ADD);
  and and_14 (and_14_out, not_33_out, Q1, not_34_out, not_35_out);
  and and_15 (and_15_out, not_36_out, Q1, not_37_out, not_38_out);
  and and_16 (and_16_out, not_39_out, not_40_out, not_41_out, PWR, not_42_out);
  and and_17 (and_17_out, not_43_out, Q0, not_44_out, not_45_out);
  and and_18 (and_18_out, not_46_out, Q1, not_47_out, not_48_out, ADD);
  or or_1 (R, and_1_out, and_2_out, and_3_out, and_4_out, and_5_out);
  or or_2 (B, and_6_out, and_7_out, and_8_out);
  or or_3 (DISPLAY, and_9_out, and_10_out, and_11_out);
  or or_4 (D1, and_13_out, and_14_out, and_15_out);
  or or_5 (D0, and_16_out, and_17_out, and_18_out);

  assign G = 1'b0;
  assign OUT = 1'b0;
endmodule

module mde2 (
  input  Q2,
  input  Q1,
  input  Q0,
  input  Comp,
  input  PWR,
  input  ADD,
  output R,
  output G,
  output B,
  output OUT,
  output DISPLAY,
  output D2,
  output D1,
  output D0
);

  wire and_1_out, and_2_out, and_3_out, and_4_out, and_5_out, and_7_out, and_8_out, and_9_out, and_11_out,
       and_12_out, and_13_out, and_14_out, and_15_out, and_16_out, and_17_out, and_18_out, and_19_out,
       and_20_out, and_21_out, not_1_out, not_2_out, not_3_out, not_4_out, not_5_out, not_6_out, not_7_out,
       not_8_out, not_9_out, not_10_out, not_11_out, not_12_out, not_13_out, not_14_out, not_15_out,
       not_16_out, not_17_out, not_18_out, not_19_out, not_20_out, not_21_out, not_22_out, not_23_out,
       not_24_out, not_25_out, not_26_out, not_27_out, not_28_out, not_29_out, not_30_out, not_31_out,
       not_32_out, not_33_out, not_34_out, not_35_out, not_36_out, not_37_out, not_38_out, not_39_out,
       not_40_out, not_41_out, not_42_out, not_43_out, not_44_out, not_45_out, not_46_out, not_47_out,
       not_48_out, not_49_out, not_50_out, not_51_out, not_52_out, not_53_out, not_54_out, not_55_out,
       not_56_out, not_57_out, not_58_out, not_59_out, not_60_out, not_61_out, not_62_out, not_63_out,
       not_64_out, not_65_out, not_66_out, not_67_out, not_68_out, not_69_out, not_70_out, not_71_out,
       not_72_out, not_73_out, not_74_out, not_75_out, not_76_out, not_77_out, not_78_out, not_79_out,
       not_80_out;

  not not_1 (not_1_out, Q2);
  not not_2 (not_2_out, Q1);
  not not_3 (not_3_out, Q0);
  not not_4 (not_4_out, Comp);
  not not_5 (not_5_out, PWR);
  not not_6 (not_6_out, Q1);
  not not_7 (not_7_out, Q0);
  not not_8 (not_8_out, Comp);
  not not_9 (not_9_out, PWR);
  not not_10 (not_10_out, ADD);
  not not_11 (not_11_out, Q2);
  not not_12 (not_12_out, Comp);
  not not_13 (not_13_out, Q2);
  not not_14 (not_14_out, Comp);
  not not_15 (not_15_out, ADD);
  not not_16 (not_16_out, Q2);
  not not_17 (not_17_out, Comp);
  not not_18 (not_18_out, ADD);
  not not_19 (not_19_out, Q1);
  not not_20 (not_20_out, Q0);
  not not_21 (not_21_out, PWR);
  not not_22 (not_22_out, ADD);
  not not_23 (not_23_out, Q2);
  not not_24 (not_24_out, Q1);
  not not_25 (not_25_out, Q0);
  not not_26 (not_26_out, Comp);
  not not_27 (not_27_out, ADD);
  not not_28 (not_28_out, Q2);
  not not_29 (not_29_out, Comp);
  not not_30 (not_30_out, PWR);
  not not_31 (not_31_out, Q2);
  not not_32 (not_32_out, Comp);
  not not_33 (not_33_out, PWR);
  not not_34 (not_34_out, Q1);
  not not_35 (not_35_out, Q0);
  not not_36 (not_36_out, PWR);
  not not_37 (not_37_out, ADD);
  not not_38 (not_38_out, Q2);
  not not_39 (not_39_out, Comp);
  not not_40 (not_40_out, PWR);
  not not_41 (not_41_out, Q2);
  not not_42 (not_42_out, Comp);
  not not_43 (not_43_out, PWR);
  not not_44 (not_44_out, Q1);
  not not_45 (not_45_out, Q0);
  not not_46 (not_46_out, PWR);
  not not_47 (not_47_out, ADD);
  not not_48 (not_48_out, Q2);
  not not_49 (not_49_out, Comp);
  not not_50 (not_50_out, PWR);
  not not_51 (not_51_out, Q1);
  not not_52 (not_52_out, Q0);
  not not_53 (not_53_out, Comp);
  not not_54 (not_54_out, PWR);
  not not_55 (not_55_out, ADD);
  not not_56 (not_56_out, Q2);
  not not_57 (not_57_out, Q1);
  not not_58 (not_58_out, Comp);
  not not_59 (not_59_out, PWR);
  not not_60 (not_60_out, Q2);
  not not_61 (not_61_out, Q0);
  not not_62 (not_62_out, Comp);
  not not_63 (not_63_out, PWR);
  not not_64 (not_64_out, Q2);
  not not_65 (not_65_out, Comp);
  not not_66 (not_66_out, PWR);
  not not_67 (not_67_out, ADD);
  not not_68 (not_68_out, Q2);
  not not_69 (not_69_out, Q1);
  not not_70 (not_70_out, Q0);
  not not_71 (not_71_out, Comp);
  not not_72 (not_72_out, ADD);
  not not_73 (not_73_out, Q2);
  not not_74 (not_74_out, Comp);
  not not_75 (not_75_out, PWR);
  not not_76 (not_76_out, ADD);
  not not_77 (not_77_out, Q2);
  not not_78 (not_78_out, Q0);
  not not_79 (not_79_out, Comp);
  not not_80 (not_80_out, PWR);
  and and_1 (and_1_out, not_1_out, not_2_out, not_3_out, not_4_out, not_5_out);
  and and_2 (and_2_out, not_6_out, not_7_out, not_8_out, not_9_out, not_10_out);
  and and_3 (and_3_out, not_11_out, not_12_out, PWR, ADD);
  and and_4 (and_4_out, not_13_out, Q0, not_14_out, not_15_out);
  and and_5 (and_5_out, not_16_out, Q1, not_17_out, not_18_out);
  and and_6 (G, Q2, not_19_out, not_20_out, Comp, not_21_out, not_22_out);
  and and_7 (and_7_out, not_23_out, not_24_out, not_25_out, not_26_out, PWR, not_27_out);
  and and_8 (and_8_out, not_28_out, Q0, not_29_out, not_30_out, ADD);
  and and_9 (and_9_out, not_31_out, Q1, not_32_out, not_33_out, ADD);
  and and_10 (OUT, Q2, not_34_out, not_35_out, Comp, not_36_out, not_37_out);
  and and_11 (and_11_out, not_38_out, Q0, not_39_out, not_40_out);
  and and_12 (and_12_out, not_41_out, Q1, not_42_out, not_43_out);
  and and_13 (and_13_out, Q2, not_44_out, not_45_out, not_46_out, not_47_out);
  and and_14 (and_14_out, not_48_out, Q1, Q0, not_49_out, not_50_out, ADD);
  and and_15 (and_15_out, Q2, not_51_out, not_52_out, not_53_out, not_54_out, not_55_out);
  and and_16 (and_16_out, not_56_out, not_57_out, Q0, not_58_out, not_59_out, ADD);
  and and_17 (and_17_out, not_60_out, Q1, not_61_out, not_62_out, not_63_out);
  and and_18 (and_18_out, not_64_out, Q1, not_65_out, not_66_out, not_67_out);
  and and_19 (and_19_out, not_68_out, not_69_out, not_70_out, not_71_out, PWR, not_72_out);
  and and_20 (and_20_out, not_73_out, Q0, not_74_out, not_75_out, not_76_out);
  and and_21 (and_21_out, not_77_out, Q1, not_78_out, not_79_out, not_80_out, ADD);
  or or_1 (R, and_1_out, and_2_out, and_3_out, and_4_out, and_5_out);
  or or_2 (B, and_7_out, and_8_out, and_9_out);
  or or_3 (DISPLAY, and_11_out, and_12_out, and_13_out);
  or or_4 (D2, and_14_out, and_15_out);
  or or_5 (D1, and_16_out, and_17_out, and_18_out);
  or or_6 (D0, and_19_out, and_20_out, and_21_out);
endmodule

module MDE2 (
  input  Q2,
  input  Q1,
  input  Q0,
  input  Comp,
  input  PWR,
  input  ADD,
  output R,
  output G,
  output B,
  output OUT,
  output DISPLAY,
  output D2,
  output D1,
  output D0
);

  wire and_1_out, and_2_out, and_3_out, and_4_out, and_5_out, and_6_out, and_8_out, and_9_out, and_10_out,
       and_11_out, and_12_out, and_13_out, and_14_out, and_15_out, and_16_out, and_18_out, and_19_out,
       and_20_out, and_21_out, and_22_out, and_23_out, not_1_out, not_2_out, not_3_out, not_4_out, not_5_out,
       not_6_out, not_7_out, not_8_out, not_9_out, not_10_out, not_11_out, not_12_out, not_13_out,
       not_14_out, not_15_out, not_16_out, not_17_out, not_18_out, not_19_out, not_20_out, not_21_out,
       not_22_out, not_23_out, not_24_out, not_25_out, not_26_out, not_27_out, not_28_out, not_29_out,
       not_30_out, not_31_out, not_32_out, not_33_out, not_34_out, not_35_out, not_36_out, not_37_out,
       not_38_out, not_39_out, not_40_out, not_41_out, not_42_out, not_43_out, not_44_out, not_45_out,
       not_46_out, not_47_out, not_48_out, not_49_out, not_50_out, not_51_out, not_52_out, not_53_out,
       not_54_out, not_55_out, not_56_out, not_57_out, not_58_out, not_59_out, not_60_out, not_61_out,
       not_62_out, not_63_out, not_64_out, not_65_out, not_66_out, not_67_out, not_68_out, not_69_out,
       not_70_out, not_71_out, not_72_out, not_73_out, not_74_out, not_75_out, not_76_out, not_77_out,
       not_78_out, not_79_out, not_80_out;

  not not_1 (not_1_out, Q2);
  not not_2 (not_2_out, Q1);
  not not_3 (not_3_out, Q0);
  not not_4 (not_4_out, Comp);
  not not_5 (not_5_out, PWR);
  not not_6 (not_6_out, Q1);
  not not_7 (not_7_out, Q0);
  not not_8 (not_8_out, Comp);
  not not_9 (not_9_out, PWR);
  not not_10 (not_10_out, ADD);
  not not_11 (not_11_out, Q2);
  not not_12 (not_12_out, Comp);
  not not_13 (not_13_out, Q2);
  not not_14 (not_14_out, Comp);
  not not_15 (not_15_out, ADD);
  not not_16 (not_16_out, Q2);
  not not_17 (not_17_out, Comp);
  not not_18 (not_18_out, ADD);
  not not_19 (not_19_out, Q2);
  not not_20 (not_20_out, PWR);
  not not_21 (not_21_out, Q1);
  not not_22 (not_22_out, Q0);
  not not_23 (not_23_out, PWR);
  not not_24 (not_24_out, ADD);
  not not_25 (not_25_out, Q2);
  not not_26 (not_26_out, Q1);
  not not_27 (not_27_out, Q0);
  not not_28 (not_28_out, Comp);
  not not_29 (not_29_out, ADD);
  not not_30 (not_30_out, Q2);
  not not_31 (not_31_out, Comp);
  not not_32 (not_32_out, PWR);
  not not_33 (not_33_out, Q2);
  not not_34 (not_34_out, Comp);
  not not_35 (not_35_out, PWR);
  not not_36 (not_36_out, Q2);
  not not_37 (not_37_out, PWR);
  not not_38 (not_38_out, Q1);
  not not_39 (not_39_out, Q0);
  not not_40 (not_40_out, PWR);
  not not_41 (not_41_out, ADD);
  not not_42 (not_42_out, Q2);
  not not_43 (not_43_out, Comp);
  not not_44 (not_44_out, PWR);
  not not_45 (not_45_out, Q2);
  not not_46 (not_46_out, Comp);
  not not_47 (not_47_out, PWR);
  not not_48 (not_48_out, Q2);
  not not_49 (not_49_out, PWR);
  not not_50 (not_50_out, Q1);
  not not_51 (not_51_out, Q0);
  not not_52 (not_52_out, PWR);
  not not_53 (not_53_out, ADD);
  not not_54 (not_54_out, Q2);
  not not_55 (not_55_out, PWR);
  not not_56 (not_56_out, Q2);
  not not_57 (not_57_out, Q1);
  not not_58 (not_58_out, Comp);
  not not_59 (not_59_out, PWR);
  not not_60 (not_60_out, Q2);
  not not_61 (not_61_out, Q0);
  not not_62 (not_62_out, Comp);
  not not_63 (not_63_out, PWR);
  not not_64 (not_64_out, Q2);
  not not_65 (not_65_out, Comp);
  not not_66 (not_66_out, PWR);
  not not_67 (not_67_out, ADD);
  not not_68 (not_68_out, Q2);
  not not_69 (not_69_out, Q1);
  not not_70 (not_70_out, Q0);
  not not_71 (not_71_out, Comp);
  not not_72 (not_72_out, ADD);
  not not_73 (not_73_out, Q2);
  not not_74 (not_74_out, Comp);
  not not_75 (not_75_out, PWR);
  not not_76 (not_76_out, ADD);
  not not_77 (not_77_out, Q2);
  not not_78 (not_78_out, Q0);
  not not_79 (not_79_out, Comp);
  not not_80 (not_80_out, PWR);
  and and_1 (and_1_out, not_1_out, not_2_out, not_3_out, not_4_out, not_5_out);
  and and_2 (and_2_out, not_6_out, not_7_out, not_8_out, not_9_out, not_10_out);
  and and_3 (and_3_out, not_11_out, not_12_out, PWR, ADD);
  and and_4 (and_4_out, not_13_out, Q0, not_14_out, not_15_out);
  and and_5 (and_5_out, not_16_out, Q1, not_17_out, not_18_out);
  and and_6 (and_6_out, not_19_out, Q1, Q0, Comp, not_20_out, ADD);
  and and_7 (G, Q2, not_21_out, not_22_out, Comp, not_23_out, not_24_out);
  and and_8 (and_8_out, not_25_out, not_26_out, not_27_out, not_28_out, PWR, not_29_out);
  and and_9 (and_9_out, not_30_out, Q0, not_31_out, not_32_out, ADD);
  and and_10 (and_10_out, not_33_out, Q1, not_34_out, not_35_out, ADD);
  and and_11 (and_11_out, not_36_out, Q1, Q0, Comp, not_37_out, ADD);
  and and_12 (and_12_out, Q2, not_38_out, not_39_out, Comp, not_40_out, not_41_out);
  and and_13 (and_13_out, not_42_out, Q0, not_43_out, not_44_out);
  and and_14 (and_14_out, not_45_out, Q1, not_46_out, not_47_out);
  and and_15 (and_15_out, not_48_out, Q1, Q0, not_49_out, ADD);
  and and_16 (and_16_out, Q2, not_50_out, not_51_out, not_52_out, not_53_out);
  and and_17 (D2, not_54_out, Q1, Q0, not_55_out, ADD);
  and and_18 (and_18_out, not_56_out, not_57_out, Q0, not_58_out, not_59_out, ADD);
  and and_19 (and_19_out, not_60_out, Q1, not_61_out, not_62_out, not_63_out);
  and and_20 (and_20_out, not_64_out, Q1, not_65_out, not_66_out, not_67_out);
  and and_21 (and_21_out, not_68_out, not_69_out, not_70_out, not_71_out, PWR, not_72_out);
  and and_22 (and_22_out, not_73_out, Q0, not_74_out, not_75_out, not_76_out);
  and and_23 (and_23_out, not_77_out, Q1, not_78_out, not_79_out, not_80_out, ADD);
  or or_1 (R, and_1_out, and_2_out, and_3_out, and_4_out, and_5_out, and_6_out);
  or or_2 (B, and_8_out, and_9_out, and_10_out);
  or or_3 (OUT, and_11_out, and_12_out);
  or or_4 (DISPLAY, and_13_out, and_14_out, and_15_out, and_16_out);
  or or_5 (D1, and_18_out, and_19_out, and_20_out);
  or or_6 (D0, and_21_out, and_22_out, and_23_out);
endmodule

module MDE3 (
  input  Q2,
  input  Q1,
  input  Q0,
  input  Comp,
  input  T20,
  input  T5,
  input  CANC,
  input  PWR,
  input  ADD,
  output R,
  output G,
  output B,
  output DIS,
  output D2,
  output D1,
  output D0,
  output TD5,
  output TD20,
  output CANC2,
  output OUT
);

  wire and_1_out, and_2_out, and_3_out, and_4_out, and_6_out, and_7_out, and_8_out, and_9_out, and_10_out,
       and_11_out, and_12_out, and_13_out, and_14_out, and_15_out, and_16_out, and_17_out, and_18_out,
       and_19_out, and_20_out, and_21_out, and_22_out, and_23_out, and_24_out, and_25_out, and_26_out,
       and_27_out, and_28_out, and_29_out, and_30_out, and_31_out, and_32_out, and_33_out, and_34_out,
       and_37_out, and_38_out, not_1_out, not_2_out, not_3_out, not_4_out, not_5_out, not_6_out, not_7_out,
       not_8_out, not_9_out, not_10_out, not_11_out, not_12_out, not_13_out, not_14_out, not_15_out,
       not_16_out, not_17_out, not_18_out, not_19_out, not_20_out, not_21_out, not_22_out, not_23_out,
       not_24_out, not_25_out, not_26_out, not_27_out, not_28_out, not_29_out, not_30_out, not_31_out,
       not_32_out, not_33_out, not_34_out, not_35_out, not_36_out, not_37_out, not_38_out, not_39_out,
       not_40_out, not_41_out, not_42_out, not_43_out, not_44_out, not_45_out, not_46_out, not_47_out,
       not_48_out, not_49_out, not_50_out, not_51_out, not_52_out, not_53_out, not_54_out, not_55_out,
       not_56_out, not_57_out, not_58_out, not_59_out, not_60_out, not_61_out, not_62_out, not_63_out,
       not_64_out, not_65_out, not_66_out, not_67_out, not_68_out, not_69_out, not_70_out, not_71_out,
       not_72_out, not_73_out, not_74_out, not_75_out, not_76_out, not_77_out, not_78_out, not_79_out,
       not_80_out, not_81_out, not_82_out, not_83_out, not_84_out, not_85_out, not_86_out, not_87_out,
       not_88_out, not_89_out, not_90_out, not_91_out, not_92_out, not_93_out, not_94_out, not_95_out,
       not_96_out, not_97_out, not_98_out, not_99_out, not_100_out, not_101_out, not_102_out, not_103_out,
       not_104_out, not_105_out, not_106_out, not_107_out, not_108_out, not_109_out, not_110_out,
       not_111_out, not_112_out, not_113_out, not_114_out, not_115_out, not_116_out, not_117_out,
       not_118_out, not_119_out, not_120_out, not_121_out, not_122_out, not_123_out, not_124_out,
       not_125_out, not_126_out, not_127_out, not_128_out, not_129_out, not_130_out, not_131_out,
       not_132_out, not_133_out, not_134_out, not_135_out, not_136_out, not_137_out, not_138_out,
       not_139_out, not_140_out, not_141_out, not_142_out, not_143_out, not_144_out, not_145_out,
       not_146_out, not_147_out, not_148_out, not_149_out, not_150_out, not_151_out, not_152_out,
       not_153_out, not_154_out, not_155_out, not_156_out, not_157_out, not_158_out, not_159_out,
       not_160_out, not_161_out, not_162_out, not_163_out, not_164_out, not_165_out, not_166_out,
       not_167_out, not_168_out, not_169_out, not_170_out, not_171_out, not_172_out, not_173_out,
       not_174_out, not_175_out, not_176_out, not_177_out, not_178_out, not_179_out, not_180_out,
       not_181_out, not_182_out, not_183_out, not_184_out, not_185_out, not_186_out, not_187_out,
       not_188_out, not_189_out, not_190_out, not_191_out, not_192_out, not_193_out, not_194_out,
       not_195_out, not_196_out, not_197_out, not_198_out, not_199_out, not_200_out, not_201_out,
       not_202_out, not_203_out, not_204_out, not_205_out, not_206_out, not_207_out, not_208_out,
       not_209_out, not_210_out, not_211_out, not_212_out, not_213_out, not_214_out, not_215_out,
       not_216_out, not_217_out, not_218_out, not_219_out, not_220_out, not_221_out, not_222_out, not_223_out;

  not not_1 (not_1_out, Q2);
  not not_2 (not_2_out, Q1);
  not not_3 (not_3_out, Comp);
  not not_4 (not_4_out, T20);
  not not_5 (not_5_out, T5);
  not not_6 (not_6_out, CANC);
  not not_7 (not_7_out, Q2);
  not not_8 (not_8_out, Comp);
  not not_9 (not_9_out, T20);
  not not_10 (not_10_out, T5);
  not not_11 (not_11_out, CANC);
  not not_12 (not_12_out, PWR);
  not not_13 (not_13_out, Q1);
  not not_14 (not_14_out, Q0);
  not not_15 (not_15_out, Comp);
  not not_16 (not_16_out, T20);
  not not_17 (not_17_out, T5);
  not not_18 (not_18_out, CANC);
  not not_19 (not_19_out, Q1);
  not not_20 (not_20_out, Q0);
  not not_21 (not_21_out, T20);
  not not_22 (not_22_out, T5);
  not not_23 (not_23_out, CANC);
  not not_24 (not_24_out, PWR);
  not not_25 (not_25_out, ADD);
  not not_26 (not_26_out, Q2);
  not not_27 (not_27_out, Q1);
  not not_28 (not_28_out, Q0);
  not not_29 (not_29_out, T5);
  not not_30 (not_30_out, CANC);
  not not_31 (not_31_out, PWR);
  not not_32 (not_32_out, ADD);
  not not_33 (not_33_out, Q2);
  not not_34 (not_34_out, Q1);
  not not_35 (not_35_out, Q0);
  not not_36 (not_36_out, Comp);
  not not_37 (not_37_out, T20);
  not not_38 (not_38_out, T5);
  not not_39 (not_39_out, PWR);
  not not_40 (not_40_out, ADD);
  not not_41 (not_41_out, Q2);
  not not_42 (not_42_out, Q1);
  not not_43 (not_43_out, Comp);
  not not_44 (not_44_out, T20);
  not not_45 (not_45_out, CANC);
  not not_46 (not_46_out, Q2);
  not not_47 (not_47_out, Comp);
  not not_48 (not_48_out, T20);
  not not_49 (not_49_out, CANC);
  not not_50 (not_50_out, PWR);
  not not_51 (not_51_out, Q1);
  not not_52 (not_52_out, Q0);
  not not_53 (not_53_out, Comp);
  not not_54 (not_54_out, T20);
  not not_55 (not_55_out, CANC);
  not not_56 (not_56_out, PWR);
  not not_57 (not_57_out, Q2);
  not not_58 (not_58_out, Comp);
  not not_59 (not_59_out, T20);
  not not_60 (not_60_out, CANC);
  not not_61 (not_61_out, Q1);
  not not_62 (not_62_out, Q0);
  not not_63 (not_63_out, T20);
  not not_64 (not_64_out, CANC);
  not not_65 (not_65_out, PWR);
  not not_66 (not_66_out, ADD);
  not not_67 (not_67_out, Q2);
  not not_68 (not_68_out, Q1);
  not not_69 (not_69_out, Comp);
  not not_70 (not_70_out, T20);
  not not_71 (not_71_out, CANC);
  not not_72 (not_72_out, ADD);
  not not_73 (not_73_out, Q2);
  not not_74 (not_74_out, Q1);
  not not_75 (not_75_out, Q0);
  not not_76 (not_76_out, Comp);
  not not_77 (not_77_out, T20);
  not not_78 (not_78_out, T5);
  not not_79 (not_79_out, PWR);
  not not_80 (not_80_out, ADD);
  not not_81 (not_81_out, Q2);
  not not_82 (not_82_out, Q1);
  not not_83 (not_83_out, Comp);
  not not_84 (not_84_out, T20);
  not not_85 (not_85_out, CANC);
  not not_86 (not_86_out, Q1);
  not not_87 (not_87_out, Q0);
  not not_88 (not_88_out, Comp);
  not not_89 (not_89_out, T20);
  not not_90 (not_90_out, CANC);
  not not_91 (not_91_out, PWR);
  not not_92 (not_92_out, Q2);
  not not_93 (not_93_out, Q1);
  not not_94 (not_94_out, Q0);
  not not_95 (not_95_out, T5);
  not not_96 (not_96_out, CANC);
  not not_97 (not_97_out, PWR);
  not not_98 (not_98_out, ADD);
  not not_99 (not_99_out, Q2);
  not not_100 (not_100_out, Q1);
  not not_101 (not_101_out, Comp);
  not not_102 (not_102_out, T20);
  not not_103 (not_103_out, CANC);
  not not_104 (not_104_out, Q2);
  not not_105 (not_105_out, Comp);
  not not_106 (not_106_out, T20);
  not not_107 (not_107_out, CANC);
  not not_108 (not_108_out, Q2);
  not not_109 (not_109_out, Comp);
  not not_110 (not_110_out, T20);
  not not_111 (not_111_out, CANC);
  not not_112 (not_112_out, PWR);
  not not_113 (not_113_out, Q1);
  not not_114 (not_114_out, Q0);
  not not_115 (not_115_out, Comp);
  not not_116 (not_116_out, T20);
  not not_117 (not_117_out, T5);
  not not_118 (not_118_out, CANC);
  not not_119 (not_119_out, Q1);
  not not_120 (not_120_out, Q0);
  not not_121 (not_121_out, T20);
  not not_122 (not_122_out, CANC);
  not not_123 (not_123_out, PWR);
  not not_124 (not_124_out, ADD);
  not not_125 (not_125_out, Q2);
  not not_126 (not_126_out, Comp);
  not not_127 (not_127_out, T20);
  not not_128 (not_128_out, T5);
  not not_129 (not_129_out, CANC);
  not not_130 (not_130_out, PWR);
  not not_131 (not_131_out, Q1);
  not not_132 (not_132_out, Q0);
  not not_133 (not_133_out, Comp);
  not not_134 (not_134_out, T20);
  not not_135 (not_135_out, CANC);
  not not_136 (not_136_out, PWR);
  not not_137 (not_137_out, Q2);
  not not_138 (not_138_out, Q1);
  not not_139 (not_139_out, Comp);
  not not_140 (not_140_out, T20);
  not not_141 (not_141_out, T5);
  not not_142 (not_142_out, CANC);
  not not_143 (not_143_out, PWR);
  not not_144 (not_144_out, Q2);
  not not_145 (not_145_out, Q0);
  not not_146 (not_146_out, Comp);
  not not_147 (not_147_out, T20);
  not not_148 (not_148_out, CANC);
  not not_149 (not_149_out, PWR);
  not not_150 (not_150_out, Q2);
  not not_151 (not_151_out, Comp);
  not not_152 (not_152_out, T20);
  not not_153 (not_153_out, CANC);
  not not_154 (not_154_out, PWR);
  not not_155 (not_155_out, ADD);
  not not_156 (not_156_out, Q2);
  not not_157 (not_157_out, Comp);
  not not_158 (not_158_out, T20);
  not not_159 (not_159_out, CANC);
  not not_160 (not_160_out, Q2);
  not not_161 (not_161_out, Q1);
  not not_162 (not_162_out, Comp);
  not not_163 (not_163_out, T20);
  not not_164 (not_164_out, CANC);
  not not_165 (not_165_out, Q2);
  not not_166 (not_166_out, Comp);
  not not_167 (not_167_out, T20);
  not not_168 (not_168_out, CANC);
  not not_169 (not_169_out, PWR);
  not not_170 (not_170_out, ADD);
  not not_171 (not_171_out, Q2);
  not not_172 (not_172_out, Comp);
  not not_173 (not_173_out, T20);
  not not_174 (not_174_out, CANC);
  not not_175 (not_175_out, Q2);
  not not_176 (not_176_out, Q0);
  not not_177 (not_177_out, Comp);
  not not_178 (not_178_out, T20);
  not not_179 (not_179_out, T5);
  not not_180 (not_180_out, CANC);
  not not_181 (not_181_out, PWR);
  not not_182 (not_182_out, Q2);
  not not_183 (not_183_out, Q1);
  not not_184 (not_184_out, Q0);
  not not_185 (not_185_out, Comp);
  not not_186 (not_186_out, T20);
  not not_187 (not_187_out, T5);
  not not_188 (not_188_out, CANC);
  not not_189 (not_189_out, ADD);
  not not_190 (not_190_out, Q2);
  not not_191 (not_191_out, Comp);
  not not_192 (not_192_out, T20);
  not not_193 (not_193_out, T5);
  not not_194 (not_194_out, CANC);
  not not_195 (not_195_out, PWR);
  not not_196 (not_196_out, Q2);
  not not_197 (not_197_out, Comp);
  not not_198 (not_198_out, T20);
  not not_199 (not_199_out, T5);
  not not_200 (not_200_out, CANC);
  not not_201 (not_201_out, PWR);
  not not_202 (not_202_out, Q1);
  not not_203 (not_203_out, Q0);
  not not_204 (not_204_out, T20);
  not not_205 (not_205_out, CANC);
  not not_206 (not_206_out, PWR);
  not not_207 (not_207_out, ADD);
  not not_208 (not_208_out, T5);
  not not_209 (not_209_out, CANC);
  not not_210 (not_210_out, Q2);
  not not_211 (not_211_out, Q1);
  not not_212 (not_212_out, Q0);
  not not_213 (not_213_out, T5);
  not not_214 (not_214_out, CANC);
  not not_215 (not_215_out, PWR);
  not not_216 (not_216_out, ADD);
  not not_217 (not_217_out, Q1);
  not not_218 (not_218_out, Q0);
  not not_219 (not_219_out, T20);
  not not_220 (not_220_out, T5);
  not not_221 (not_221_out, CANC);
  not not_222 (not_222_out, PWR);
  not not_223 (not_223_out, ADD);
  and and_1 (and_1_out, not_1_out, not_2_out, not_3_out, not_4_out, not_5_out, not_6_out);
  and and_2 (and_2_out, not_7_out, not_8_out, not_9_out, not_10_out, not_11_out, not_12_out);
  and and_3 (and_3_out, not_13_out, not_14_out, not_15_out, not_16_out, not_17_out, not_18_out);
  and and_4 (and_4_out, Q2, not_19_out, not_20_out, not_21_out, not_22_out, not_23_out, not_24_out, not_25_out);
  and and_5 (G, not_26_out, not_27_out, not_28_out, T20, not_29_out, not_30_out, not_31_out, not_32_out);
  and and_6 (and_6_out, not_33_out, not_34_out, not_35_out, not_36_out, not_37_out, not_38_out, CANC, not_39_out, not_40_out);
  and and_7 (and_7_out, not_41_out, not_42_out, not_43_out, not_44_out, T5, not_45_out);
  and and_8 (and_8_out, not_46_out, not_47_out, not_48_out, T5, not_49_out, not_50_out);
  and and_9 (and_9_out, not_51_out, not_52_out, not_53_out, not_54_out, T5, not_55_out, not_56_out);
  and and_10 (and_10_out, not_57_out, Q0, not_58_out, not_59_out, T5, not_60_out);
  and and_11 (and_11_out, Q2, not_61_out, not_62_out, not_63_out, T5, not_64_out, not_65_out, not_66_out);
  and and_12 (and_12_out, not_67_out, not_68_out, not_69_out, not_70_out, not_71_out, PWR, not_72_out);
  and and_13 (and_13_out, not_73_out, not_74_out, not_75_out, not_76_out, not_77_out, not_78_out, CANC, not_79_out, not_80_out);
  and and_14 (and_14_out, not_81_out, not_82_out, not_83_out, not_84_out, T5, not_85_out);
  and and_15 (and_15_out, not_86_out, not_87_out, not_88_out, not_89_out, T5, not_90_out, not_91_out);
  and and_16 (and_16_out, not_92_out, not_93_out, not_94_out, T20, not_95_out, not_96_out, not_97_out, not_98_out);
  and and_17 (and_17_out, not_99_out, not_100_out, Q0, not_101_out, not_102_out, not_103_out);
  and and_18 (and_18_out, not_104_out, Q0, not_105_out, not_106_out, T5, not_107_out);
  and and_19 (and_19_out, not_108_out, Q1, not_109_out, not_110_out, not_111_out, not_112_out);
  and and_20 (and_20_out, Q2, not_113_out, not_114_out, not_115_out, not_116_out, not_117_out, not_118_out);
  and and_21 (and_21_out, Q2, not_119_out, not_120_out, not_121_out, not_122_out, not_123_out, not_124_out);
  and and_22 (and_22_out, not_125_out, Q1, Q0, not_126_out, not_127_out, not_128_out, not_129_out, not_130_out, ADD);
  and and_23 (and_23_out, Q2, not_131_out, not_132_out, not_133_out, not_134_out, T5, not_135_out, not_136_out);
  and and_24 (and_24_out, not_137_out, not_138_out, Q0, not_139_out, not_140_out, not_141_out, not_142_out, not_143_out, ADD);
  and and_25 (and_25_out, not_144_out, Q1, not_145_out, not_146_out, not_147_out, not_148_out, not_149_out);
  and and_26 (and_26_out, not_150_out, Q1, not_151_out, not_152_out, not_153_out, not_154_out, not_155_out);
  and and_27 (and_27_out, not_156_out, Q1, Q0, not_157_out, not_158_out, T5, not_159_out);
  and and_28 (and_28_out, not_160_out, not_161_out, not_162_out, not_163_out, T5, not_164_out);
  and and_29 (and_29_out, not_165_out, Q0, not_166_out, not_167_out, not_168_out, not_169_out, not_170_out);
  and and_30 (and_30_out, not_171_out, Q0, not_172_out, not_173_out, T5, not_174_out);
  and and_31 (and_31_out, not_175_out, Q1, not_176_out, not_177_out, not_178_out, not_179_out, not_180_out, not_181_out, ADD);
  and and_32 (and_32_out, not_182_out, not_183_out, not_184_out, not_185_out, not_186_out, not_187_out, not_188_out, PWR, not_189_out);
  and and_33 (and_33_out, not_190_out, Q0, not_191_out, not_192_out, not_193_out, not_194_out, not_195_out, ADD);
  and and_34 (and_34_out, not_196_out, Q1, not_197_out, not_198_out, not_199_out, not_200_out, not_201_out, ADD);
  and and_35 (TD20, Q2, not_202_out, not_203_out, Comp, not_204_out, not_205_out, not_206_out, not_207_out);
  and and_36 (CANC2, Q0, not_208_out, not_209_out, PWR);
  and and_37 (and_37_out, not_210_out, not_211_out, not_212_out, T20, not_213_out, not_214_out, not_215_out, not_216_out);
  and and_38 (and_38_out, Q2, not_217_out, not_218_out, Comp, not_219_out, not_220_out, not_221_out, not_222_out, not_223_out);
  or or_1 (R, and_1_out, and_2_out, and_3_out, and_4_out);
  or or_2 (B, and_6_out, and_7_out, and_8_out, and_9_out, and_10_out, and_11_out);
  or or_3 (DIS, and_12_out, and_13_out, and_14_out, and_15_out, and_16_out, and_17_out, and_18_out, and_19_out, and_20_out, and_21_out);
  or or_4 (D2, and_22_out, and_23_out);
  or or_5 (D1, and_24_out, and_25_out, and_26_out, and_27_out);
  or or_6 (D0, and_28_out, and_29_out, and_30_out, and_31_out);
  or or_7 (TD5, and_32_out, and_33_out, and_34_out);
  or or_8 (OUT, and_37_out, and_38_out);
endmodule

module STORE (
  input  in_1,
  input  in_2,
  input  in_3,
  input  in_4,
  input  in_5,
  input  in_6,
  input  in_7,
  input  in_8,
  input  in_9,
  input  in_10,
  output out_11,
  output out_12,
  output out_13,
  output out_14,
  output out_15,
  output out_16,
  output out_17,
  output out_18,
  output out_19,
  output out_20,
  output out_21,
  output out_22,
  output out_23,
  output out_24,
  output out_25,
  output out_26,
  output out_27,
  output out_28
);

  wire and_19_out, and_20_out, and_21_out, S0, S1, S2, S3, S4, S5, S6, S7, S8, S9, S10, S11, S12, S13, S14,
       S15, S16, S17;

  and and_1 (S0, in_6, in_7, ~in_8);  // AND_Gate
  and and_2 (S1, in_5, in_7, ~in_8);  // AND_Gate
  and and_3 (S2, in_4, in_7, ~in_8);  // AND_Gate
  and and_4 (S3, in_3, in_7, ~in_8);  // AND_Gate
  and and_5 (S4, in_2, in_7, ~in_8);  // AND_Gate
  and and_6 (S5, in_1, in_7, ~in_8);  // AND_Gate
  and and_7 (S6, in_6, ~in_7, in_8);  // AND_Gate
  and and_8 (S7, in_5, ~in_7, in_8);  // AND_Gate
  and and_9 (S8, in_4, ~in_7, in_8);  // AND_Gate
  and and_10 (S9, in_3, ~in_7, in_8);  // AND_Gate
  and and_11 (S10, in_2, ~in_7, in_8);  // AND_Gate
  and and_12 (S11, in_1, ~in_7, in_8);  // AND_Gate
  and and_13 (S12, in_6, in_7, in_8);
  and and_14 (S13, in_5, in_7, in_8);
  and and_15 (S14, in_4, in_7, in_8);
  and and_16 (S15, in_3, in_7, in_8);
  and and_17 (S16, in_2, in_7, in_8);
  and and_18 (S17, in_1, in_7, in_8);
  and and_19 (and_19_out, ~in_8, in_7);  // AND_Gate
  and and_20 (and_20_out, in_8, ~in_7);  // AND_Gate
  and and_21 (and_21_out, in_8, in_7);
  Register #(.width(6), .Select("low")) register_1 (
    .D({S5, S4, S3, S2, S1, S0}), .en(and_19_out), .Q({out_16, out_15, out_14, out_13, out_12, out_11}),
    .clk(in_9), .clr(in_10));
  Register #(.width(6), .Select("low")) register_2 (
    .D({S11, S10, S9, S8, S7, S6}), .en(and_20_out), .Q({out_22, out_21, out_20, out_19, out_18, out_17}),
    .clk(in_9), .clr(in_10), .preset(in_10));  // open: cs
  Register #(.width(6), .Select("low")) register_3 (
    .D({S17, S16, S15, S14, S13, S12}), .en(and_21_out),
    .Q({out_28, out_27, out_26, out_25, out_24, out_23}), .clk(in_9), .clr(in_10), .preset(in_10));  // open: cs

  // Other names for the same wires on the sheet: A = in_7; B = in_8; B0 = in_6; B1 = in_5; B2 = in_4; B3 = in_3;
  //   B4 = in_2; B5 = in_1; CLK = in_9
endmodule

module COMP_18 (
  input  in_1,
  input  in_2,
  input  in_3,
  input  in_4,
  input  in_5,
  input  in_6,
  input  in_7,
  input  in_8,
  input  in_9,
  input  in_10,
  input  in_11,
  input  in_12,
  input  in_13,
  input  in_14,
  input  in_15,
  input  in_16,
  input  in_17,
  input  in_18,
  input  in_19,
  input  in_20,
  input  in_21,
  input  in_22,
  input  in_23,
  input  in_24,
  input  in_25,
  input  in_26,
  input  in_27,
  input  in_28,
  input  in_29,
  input  in_30,
  input  in_31,
  input  in_32,
  input  in_33,
  input  in_34,
  input  in_35,
  input  in_36,
  output out_37
);

  Comparator #(.width(18), .mode("unsigned")) comparator_1 (
    .a({in_36, in_34, in_32, in_30, in_28, in_26, in_24, in_22, in_20, in_18, in_16, in_14, in_12, in_10, in_8, in_6, in_4, in_2}),
    .b({in_35, in_33, in_31, in_29, in_27, in_25, in_23, in_21, in_19, in_17, in_15, in_13, in_11, in_9, in_7, in_5, in_3, in_1}),
    .eq(out_37));  // open: gt, lt
endmodule
