// Logisim project TEO09.circ as structural Verilog: 5 circuits, main circuit main
module main (
  input  C6,
  input  C5,
  input  C4,
  input  C3,
  input  C2,
  input  C1,
  input  in_7,
  input  COMP,
  input  in_9,
  input  RST,
  input  [9:0] in_11,
  input  in_12,
  output [9:0] out_13,
  output [9:0] out_14,
  output [9:0] out_15,
  output [9:0] out_16,
  output [9:0] out_17,
  output [9:0] out_18
);

  wire and_1_out, CLK, COMP_t, D0, D1, D2, divisor_1_comp, divisor_1_out_5, mde_1_i1, not_1_out, Q0, Q1, Q2,
       RST_t, TEM;

  not not_1 (not_1_out, and_1_out);
  and and_1 (and_1_out, ~Q2, ~Q1, ~Q0);  // AND_Gate
  Divisor divisor_1 (
    .in_1(CLK), .INPUT(in_11), .in_3({Q2, Q1, Q0}), .in_4(in_12), .out_5(divisor_1_out_5),
    .COMP(divisor_1_comp), .out_8(out_13), .out_9(out_14), .out_10(out_15), .out_11(out_16), .out_12(out_17),
    .out_13(out_18));  // open: out_7
  NBNBM nbnbm_1 (.C6(C6), .C5(C5), .C4(C4), .C3(C3), .C2(C2), .C1(C1), .in_1(1'b0), .in_8({Q2, Q1, Q0}), .TEM(TEM));
  Multiplexer #(.enable("false")) multiplexer_1 (.in0(in_9), .in1(divisor_1_out_5), .out(COMP_t), .sel(not_1_out));
  Multiplexer #(.enable("false")) multiplexer_2 (.in0(in_9), .in1(divisor_1_comp), .out(RST_t), .sel(not_1_out));
  Clock clock_1 (.out(CLK));
  MDE mde_1 (
    .Q2(Q2), .Q1(Q1), .Q0(Q0), .T(in_7), .TEM(TEM), .COMP(COMP_t), .RESTO(RST_t), .D2(D2), .D1(D1), .D0(D0),
    .I1(mde_1_i1));  // open: I2, I3, I4, I5, I6, L
  D_Flip_Flop d_ff_1 (.clk(CLK), .D(D2), .Q(Q2));  // open: Qn, preset, reset
  D_Flip_Flop d_ff_2 (.clk(CLK), .D(D1), .Q(Q1));  // open: Qn, preset, reset
  D_Flip_Flop d_ff_3 (.clk(CLK), .D(D0), .Q(Q0));  // open: Qn, preset, reset

  // Other names for the same wires on the sheet: S1[9:0] = out_13; S2[9:0] = out_14; S3[9:0] = out_15;
  //   S4[9:0] = out_16; S5[9:0] = out_17; S6[9:0] = out_18
endmodule

module Divisor (
  input  in_1,
  input  [9:0] INPUT,
  input  [2:0] in_3,
  input  in_4,
  output out_5,
  output COMP,
  output [9:0] out_7,
  output [9:0] out_8,
  output [9:0] out_9,
  output [9:0] out_10,
  output [9:0] out_11,
  output [9:0] out_12,
  output [9:0] out_13
);

  wire and_1_out, and_2_out, and_3_out, and_4_out, and_5_out, and_6_out, KEY, not_1_out;
  wire [9:0] multiplexer_1_out, register_1_q, RST, SM;

  Multiplexer #(.select(3), .width(10), .enable("false")) multiplexer_1 (
    .in1(10'h64), .in2(10'h32), .in3(10'h19), .in4(10'ha), .in5(10'h5), .in6(10'h1), .out(multiplexer_1_out),
    .sel(in_3));  // open: in0, in7
  Register #(.width(10), .Select("low")) register_1 (.D(RST), .Q(register_1_q), .clk(in_1));  // open: en, clr
  Multiplexer #(.width(10), .enable("false")) multiplexer_2 (.in0(INPUT), .in1(register_1_q), .out(SM), .sel(KEY));
  Divider #(.width(10)) divider_1 (.a(SM), .b(multiplexer_1_out), .out(out_7), .rem(RST));  // open: upper
  Comparator #(.width(10), .mode("unsigned")) comparator_1 (.a(RST), .b({10{1'b0}}), .eq(out_5));  // open: gt, lt
  not not_1 (not_1_out, out_5);
  Register #(.width(10), .Select("low")) register_2 (.D(out_7), .en(and_1_out), .Q(out_8), .clk(in_1), .clr(in_4));
  and and_1 (and_1_out, in_3[0], ~in_3[1], ~in_3[2]);  // AND_Gate
  Register #(.width(10), .Select("low")) register_3 (
    .D(out_7), .en(and_2_out), .Q(out_9), .clk(in_1), .clr(in_4), .preset(in_4));  // open: cs
  and and_2 (and_2_out, ~in_3[0], in_3[1], ~in_3[2]);  // AND_Gate
  Register #(.width(10), .Select("low")) register_4 (
    .D(out_7), .en(and_3_out), .Q(out_10), .clk(in_1), .clr(in_4), .preset(in_4));  // open: cs
  and and_3 (and_3_out, in_3[0], in_3[1], ~in_3[2]);  // AND_Gate
  Register #(.width(10), .Select("low")) register_5 (
    .D(out_7), .en(and_4_out), .Q(out_11), .clk(in_1), .clr(in_4), .preset(in_4));  // open: cs
  and and_4 (and_4_out, ~in_3[0], ~in_3[1], in_3[2]);  // AND_Gate
  Register #(.width(10), .Select("low")) register_6 (
    .D(out_7), .en(and_5_out), .Q(out_12), .clk(in_1), .clr(in_4), .preset(in_4));  // open: cs
  and and_5 (and_5_out, in_3[0], ~in_3[1], in_3[2]);  // AND_Gate
  Register #(.width(10), .Select("low")) register_7 (
    .D(out_7), .en(and_6_out), .Q(out_13), .clk(in_1), .clr(in_4), .preset(in_4));  // open: cs
  and and_6 (and_6_out, ~in_3[0], in_3[1], in_3[2]);  // AND_Gate
  D_Flip_Flop d_ff_1 (.clk(in_1), .D(not_1_out), .Q(KEY));  // open: Qn, preset, reset
  Comparator #(.width(10), .mode("unsigned")) comparator_2 (.a(SM), .b(RST), .eq(COMP));  // open: gt, lt

  // Other names for the same wires on the sheet: CLK = in_1; QNT[9:0] = out_7

  // Notes on the sheet:
  //   1 REAL
  //   0,50 REAL
  //   0,25 REAL
  //   0,10 REAL
  //   0,5 REAL
  //   0,01 REAL
  //   1 REAL
  //   0,50 REAL
  //   0,25 REAL
  //   0,10 REAL
  //   0,5 REAL
  //   0,01 REAL
endmodule

module logica (
  input  PWR,
  input  Q2,
  input  Q1,
  input  Q0,
  input  C6,
  input  C5,
  input  C4,
  input  C3,
  input  C2,
  input  C1,
  input  RST,
  output D2,
  output D1,
  output D0,
  output I6,
  output I5,
  output I4,
  output I3,
  output I2,
  output I1,
  output R,
  output G,
  output B
);

  wire not_1_out, not_2_out, not_3_out, not_4_out, not_5_out, not_6_out, not_7_out, not_8_out, not_9_out,
       not_10_out, not_11_out, not_12_out, not_13_out, not_14_out, not_15_out, not_16_out, not_17_out,
       not_18_out, not_19_out, not_20_out;

  not not_1 (not_1_out, Q2);
  not not_2 (not_2_out, Q1);
  not not_3 (not_3_out, Q0);
  not not_4 (not_4_out, C6);
  not not_5 (not_5_out, C5);
  not not_6 (not_6_out, C4);
  not not_7 (not_7_out, C3);
  not not_8 (not_8_out, C2);
  not not_9 (not_9_out, C1);
  not not_10 (not_10_out, RST);
  not not_11 (not_11_out, Q2);
  not not_12 (not_12_out, Q1);
  not not_13 (not_13_out, Q0);
  not not_14 (not_14_out, C6);
  not not_15 (not_15_out, C5);
  not not_16 (not_16_out, C4);
  not not_17 (not_17_out, C3);
  not not_18 (not_18_out, C2);
  not not_19 (not_19_out, C1);
  not not_20 (not_20_out, RST);
  and and_1 (D0, PWR, not_1_out, not_2_out, not_3_out, not_4_out, not_5_out, not_6_out, not_7_out, not_8_out, not_9_out, not_10_out);
  and and_2 (B, PWR, not_11_out, not_12_out, not_13_out, not_14_out, not_15_out, not_16_out, not_17_out, not_18_out, not_19_out, not_20_out);

  assign D1 = 1'b0;
  assign D2 = 1'b0;
  assign G = 1'b0;
  assign I1 = 1'b0;
  assign I2 = 1'b0;
  assign I3 = 1'b0;
  assign I4 = 1'b0;
  assign I5 = 1'b0;
  assign I6 = 1'b0;
  assign R = 1'b0;
endmodule

module NBNBM (
  input  in_1,
  input  C6,
  input  C5,
  input  C4,
  input  C3,
  input  C2,
  input  C1,
  input  [2:0] in_8,
  output TEM
);

  Multiplexer #(.select(3), .enable("false")) multiplexer_1 (
    .in0(in_1), .in1(C6), .in2(C5), .in3(C4), .in4(C3), .in5(C2), .in6(C1), .in7(1'b0), .out(TEM), .sel(in_8));
endmodule

module MDE (
  input  Q2,
  input  Q1,
  input  Q0,
  input  T,
  input  TEM,
  input  COMP,
  input  RESTO,
  output D2,
  output D1,
  output D0,
  output I1,
  output I2,
  output I3,
  output I4,
  output I5,
  output I6,
  output L
);

  wire and_1_out, and_2_out, and_3_out, and_4_out, and_5_out, and_6_out, and_7_out, and_8_out, and_9_out,
       and_10_out, and_11_out, and_12_out, and_13_out, and_14_out, and_15_out, and_16_out, and_17_out,
       and_18_out, and_19_out, and_20_out, and_21_out, and_22_out, and_23_out, and_24_out, and_25_out,
       and_26_out, and_27_out, and_28_out, and_29_out, and_30_out, and_31_out, and_32_out, not_1_out,
       not_2_out, not_3_out, not_4_out, not_5_out, not_6_out, not_7_out, not_8_out, not_9_out, not_10_out,
       not_11_out, not_12_out, not_13_out, not_14_out, not_15_out, not_16_out, not_17_out, not_18_out,
       not_19_out, not_20_out, not_21_out, not_22_out, not_23_out, not_24_out, not_25_out, not_26_out,
       not_27_out, not_28_out, not_29_out, not_30_out, not_31_out, not_32_out, not_33_out, not_34_out,
       not_35_out, not_36_out, not_37_out, not_38_out, not_39_out, not_40_out, not_41_out, not_42_out,
       not_43_out, not_44_out, not_45_out, not_46_out, not_47_out, not_48_out, not_49_out, not_50_out,
       not_51_out, not_52_out, not_53_out, not_54_out, not_55_out, not_56_out, not_57_out, not_58_out,
       not_59_out, not_60_out, not_61_out, not_62_out, not_63_out, not_64_out, not_65_out, not_66_out,
       not_67_out;

  not not_1 (not_1_out, Q2);
  not not_2 (not_2_out, RESTO);
  not not_3 (not_3_out, Q2);
  not not_4 (not_4_out, Q1);
  not not_5 (not_5_out, Q2);
  not not_6 (not_6_out, RESTO);
  not not_7 (not_7_out, Q0);
  not not_8 (not_8_out, T);
  not not_9 (not_9_out, RESTO);
  not not_10 (not_10_out, Q0);
  not not_11 (not_11_out, RESTO);
  not not_12 (not_12_out, COMP);
  not not_13 (not_13_out, Q1);
  not not_14 (not_14_out, Q2);
  not not_15 (not_15_out, Q0);
  not not_16 (not_16_out, Q2);
  not not_17 (not_17_out, RESTO);
  not not_18 (not_18_out, Q2);
  not not_19 (not_19_out, TEM);
  not not_20 (not_20_out, Q0);
  not not_21 (not_21_out, RESTO);
  not not_22 (not_22_out, Q0);
  not not_23 (not_23_out, TEM);
  not not_24 (not_24_out, Q2);
  not not_25 (not_25_out, Q0);
  not not_26 (not_26_out, Q1);
  not not_27 (not_27_out, Q0);
  not not_28 (not_28_out, Q2);
  not not_29 (not_29_out, Q0);
  not not_30 (not_30_out, Q2);
  not not_31 (not_31_out, RESTO);
  not not_32 (not_32_out, Q1);
  not not_33 (not_33_out, RESTO);
  not not_34 (not_34_out, Q0);
  not not_35 (not_35_out, RESTO);
  not not_36 (not_36_out, RESTO);
  not not_37 (not_37_out, COMP);
  not not_38 (not_38_out, Q2);
  not not_39 (not_39_out, RESTO);
  not not_40 (not_40_out, Q2);
  not not_41 (not_41_out, COMP);
  not not_42 (not_42_out, Q2);
  not not_43 (not_43_out, TEM);
  not not_44 (not_44_out, Q2);
  not not_45 (not_45_out, RESTO);
  not not_46 (not_46_out, Q2);
  not not_47 (not_47_out, COMP);
  not not_48 (not_48_out, Q1);
  not not_49 (not_49_out, Q0);
  not not_50 (not_50_out, RESTO);
  not not_51 (not_51_out, Q1);
  not not_52 (not_52_out, Q0);
  not not_53 (not_53_out, COMP);
  not not_54 (not_54_out, Q1);
  not not_55 (not_55_out, RESTO);
  not not_56 (not_56_out, Q1);
  not not_57 (not_57_out, COMP);
  not not_58 (not_58_out, Q1);
  not not_59 (not_59_out, TEM);
  not not_60 (not_60_out, Q0);
  not not_61 (not_61_out, RESTO);
  not not_62 (not_62_out, Q0);
  not not_63 (not_63_out, TEM);
  not not_64 (not_64_out, Q2);
  not not_65 (not_65_out, Q1);
  not not_66 (not_66_out, Q0);
  not not_67 (not_67_out, T);
  and and_1 (and_1_out, not_1_out, Q1, TEM, not_2_out);
  and and_2 (and_2_out, not_3_out, Q1, Q0);
  and and_3 (and_3_out, Q2, not_4_out);
  and and_4 (and_4_out, not_5_out, Q0, TEM, not_6_out);
  and and_5 (and_5_out, Q1, not_7_out, not_8_out, TEM, not_9_out);
  and and_6 (and_6_out, Q1, not_10_out, TEM, not_11_out, not_12_out);
  and and_7 (and_7_out, not_13_out, Q0);
  and and_8 (and_8_out, not_14_out, Q1, not_15_out);
  and and_9 (and_9_out, not_16_out, Q0, TEM, not_17_out);
  and and_10 (and_10_out, not_18_out, Q0, T, not_19_out);
  and and_11 (and_11_out, Q2, not_20_out, TEM, not_21_out);
  and and_12 (and_12_out, Q2, not_22_out, T, not_23_out);
  and and_13 (and_13_out, not_24_out, Q1, not_25_out);
  and and_14 (and_14_out, Q2, not_26_out, not_27_out);
  and and_15 (and_15_out, not_28_out, not_29_out, T);
  and and_16 (and_16_out, not_30_out, Q0, TEM, not_31_out);
  and and_17 (and_17_out, not_32_out, Q0, TEM, not_33_out);
  and and_18 (and_18_out, Q1, not_34_out, TEM, not_35_out);
  and and_19 (and_19_out, Q0, TEM, not_36_out);
  and and_20 (and_20_out, Q0, TEM, not_37_out);
  and and_21 (and_21_out, not_38_out, Q1, TEM, not_39_out);
  and and_22 (and_22_out, not_40_out, Q1, TEM, not_41_out);
  and and_23 (and_23_out, not_42_out, Q1, T, not_43_out);
  and and_24 (and_24_out, not_44_out, Q1, TEM, not_45_out);
  and and_25 (and_25_out, not_46_out, Q0, TEM, RESTO, not_47_out);
  and and_26 (and_26_out, Q2, not_48_out, not_49_out, TEM, not_50_out);
  and and_27 (and_27_out, Q2, not_51_out, not_52_out, TEM, not_53_out);
  and and_28 (and_28_out, Q2, not_54_out, Q0, TEM, not_55_out);
  and and_29 (and_29_out, Q2, not_56_out, Q0, TEM, not_57_out);
  and and_30 (and_30_out, Q2, not_58_out, Q0, T, not_59_out);
  and and_31 (and_31_out, Q2, Q1, not_60_out, TEM, not_61_out);
  and and_32 (and_32_out, Q2, Q1, not_62_out, T, not_63_out);
  and and_33 (L, not_64_out, not_65_out, not_66_out, not_67_out);
  or or_1 (D2, and_1_out, and_2_out, and_3_out, and_4_out, and_5_out, and_6_out);
  or or_2 (D1, and_7_out, and_8_out, and_9_out, and_10_out, and_11_out, and_12_out);
  or or_3 (D0, and_13_out, and_14_out, and_15_out, and_16_out, and_17_out, and_18_out);
  or or_4 (I1, and_19_out, and_20_out);
  or or_5 (I2, and_21_out, and_22_out, and_23_out);
  or or_6 (I3, and_24_out, and_25_out);
  or or_7 (I4, and_26_out, and_27_out);
  or or_8 (I5, and_28_out, and_29_out, and_30_out);
  or or_9 (I6, and_31_out, and_32_out);
endmodule
