// Logisim project TEO10.circ as structural Verilog: 1 circuit, main circuit main
module main (
  input  [10:0] in_1,
  input  [2:0] in_2
);

  wire CLK, STR1, STR5, STR10, STR25, STR50, STR100;
  wire [10:0] adder_1_out, adder_2_out, adder_3_out, adder_4_out, adder_5_out, adder_6_out, adder_7_out,
       multiplexer_1_out, register_1_q;

  Adder #(.width(11)) adder_1 (.a(register_1_q), .b(11'h64), .out(adder_1_out), .cin(1'b0));  // open: cout
  Adder #(.width(11)) adder_2 (.a(register_1_q), .b(11'h32), .out(adder_2_out), .cin(1'b0));  // open: cout
  Adder #(.width(11)) adder_3 (.a(register_1_q), .b(11'h19), .out(adder_3_out), .cin(1'b0));  // open: cout
  Adder #(.width(11)) adder_4 (.a(register_1_q), .b(11'ha), .out(adder_4_out), .cin(1'b0));  // open: cout
  Adder #(.width(11)) adder_5 (.a(register_1_q), .b(11'h5), .out(adder_5_out), .cin(1'b0));  // open: cout
  Adder #(.width(11)) adder_6 (.a(register_1_q), .b(11'h1), .out(adder_6_out), .cin(1'b0));  // open: cout
  Clock clock_1 (.out(CLK));
  Comparator #(.width(11), .mode("unsigned")) comparator_1 (.a(in_1), .b(adder_1_out), .gt(STR100));  // open: eq, lt
  Comparator #(.width(11), .mode("unsigned")) comparator_2 (.a(in_1), .b(adder_2_out), .gt(STR50));  // open: eq, lt
  Comparator #(.width(11), .mode("unsigned")) comparator_3 (.a(in_1), .b(adder_3_out), .gt(STR25));  // open: eq, lt
  Comparator #(.width(11), .mode("unsigned")) comparator_4 (.a(in_1), .b(adder_4_out), .gt(STR10));  // open: eq, lt
  Comparator #(.width(11), .mode("unsigned")) comparator_5 (.a(in_1), .b(adder_5_out), .gt(STR5));  // open: eq, lt
  Comparator #(.width(11), .mode("unsigned")) comparator_6 (.a(in_1), .b(adder_6_out), .gt(STR1));  // open: eq, lt
  Multiplexer #(.select(3), .width(11), .enable("false")) multiplexer_1 (
    .in0(11'h64), .in1(11'h32), .in2(11'h19), .in3(11'ha), .in4(11'h5), .in5(11'h1), .out(multiplexer_1_out),
    .sel(in_2));  // open: in6, in7
  Register #(.width(11), .Select("low")) register_1 (.D(adder_7_out), .Q(register_1_q), .clk(CLK));  // open: en, clr
  Adder #(.width(11)) adder_7 (.a(register_1_q), .b(multiplexer_1_out), .out(adder_7_out));  // open: cin, cout
  Comparator #(.width(11), .mode("unsigned")) comparator_7 (.a(register_1_q), .b(in_1));  // open: gt, eq, lt

  // Notes on the sheet:
  //   in_1: pull=up
  //   1 REAL
  //   0,50 REAL
  //   0,25 REAL
  //   0,10 REAL
  //   0,5 REAL
  //   0,01 REAL
endmodule
